// Logisim project Alu8.circ as structural Verilog
module AluSimple8Bit (
  input  OP,
  input  [7:0] A,
  input  [7:0] B,
  output [7:0] Res,
  output C_out,
  output V_out
);

  wire and_1_out, and_2_out;
  wire [7:0] add8bit_1_res, multiplexer_1_out, not_1_out;

  // Probe on A
  // Probe on A
  assign not_1_out = ~B;  // NOT_Gate not_1, 8 bits wide
  Multiplexer #(.width(8)) multiplexer_1 (.in0(B), .in1(not_1_out), .out(multiplexer_1_out), .sel(OP));
  Add8Bit add8bit_1 (.c_in(OP), .A(A), .B(multiplexer_1_out), .Res(add8bit_1_res), .c_out(C_out));
  Multiplexer #(.width(8)) multiplexer_2 (.in0(add8bit_1_res), .in1(add8bit_1_res), .out(Res), .sel(OP));
  and and_1 (and_1_out, ~A[7], ~multiplexer_1_out[7], Res[7]);  // AND_Gate
  and and_2 (and_2_out, A[7], multiplexer_1_out[7], ~Res[7]);  // AND_Gate
  or or_1 (V_out, and_1_out, and_2_out);
endmodule

module Add8Bit (
  input  c_in,
  input  [7:0] A,
  input  [7:0] B,
  output [7:0] Res,
  output c_out
);

  wire add4bit_1_c_out;

  Add4Bit add4bit_1 (.c_in(c_in), .A(A[3:0]), .B(B[3:0]), .Res(Res[3:0]), .c_out(add4bit_1_c_out));
  Add4Bit add4bit_2 (.c_in(add4bit_1_c_out), .A(A[7:4]), .B(B[7:4]), .Res(Res[7:4]), .c_out(c_out));
endmodule

module Add1Bit (
  input  a,
  input  b,
  input  c_in,
  output Res,
  output c_out
);

  wire and_1_out, and_2_out, and_3_out, and_4_out, or_1_out, xnor_1_out, xor_1_out;

  xnor xnor_1 (xnor_1_out, a, b);
  xor xor_1 (xor_1_out, b, a);
  or or_1 (or_1_out, b, c_in);
  and and_1 (and_1_out, xnor_1_out, c_in);
  and and_2 (and_2_out, xor_1_out, ~c_in);  // AND_Gate
  and and_3 (and_3_out, or_1_out, a);
  and and_4 (and_4_out, b, c_in);
  or or_2 (Res, and_1_out, and_2_out);
  or or_3 (c_out, and_3_out, and_4_out);
endmodule

module Add2Bit (
  input  [1:0] A,
  input  c_in,
  input  [1:0] B,
  output [1:0] Res,
  output c_out
);

  wire Add1Bit0_c_out;

  Add1Bit Add1Bit0 (.a(A[0]), .b(B[0]), .c_in(c_in), .Res(Res[0]), .c_out(Add1Bit0_c_out));
  Add1Bit Add1Bit1 (.a(A[1]), .b(B[1]), .c_in(Add1Bit0_c_out), .Res(Res[1]), .c_out(c_out));
endmodule

module Add4Bit (
  input  c_in,
  input  [3:0] A,
  input  [3:0] B,
  output [3:0] Res,
  output c_out
);

  wire add2bit_1_c_out;

  Add2Bit add2bit_1 (.A(A[1:0]), .c_in(c_in), .B(B[1:0]), .Res(Res[1:0]), .c_out(add2bit_1_c_out));
  Add2Bit add2bit_2 (.A(A[3:2]), .c_in(add2bit_1_c_out), .B(B[3:2]), .Res(Res[3:2]), .c_out(c_out));
endmodule

module AluComplexe8Bit (
  input  [2:0] OP,
  input  [7:0] A,
  input  [7:0] B,
  output V_Out,
  output [7:0] Res,
  output C_out,
  output N_out,
  output Z_out
);

  wire alusimple8bit_1_c_out, decalagedroite_1_c_out, decalagegauche_1_c_out, V_Out_Add_Sub, V_Out_Decal;
  wire [7:0] aandb_1_res, alusimple8bit_1_res, aorb_1_res, decalagearidroite_1_res, decalagedroite_1_res,
       decalagegauche_1_res, nota_1_res;

  AluSimple8Bit alusimple8bit_1 (
    .OP(OP[0]), .A(A), .B(B), .Res(alusimple8bit_1_res), .C_out(alusimple8bit_1_c_out), .V_out(V_Out_Add_Sub));
  DecalageGauche decalagegauche_1 (
    .A(A), .Res(decalagegauche_1_res), .C_out(decalagegauche_1_c_out), .V_out(V_Out_Decal));
  DecalageDroite decalagedroite_1 (.A(A), .Res(decalagedroite_1_res), .C_out(decalagedroite_1_c_out));
  DecalageAriDroite decalagearidroite_1 (.A(A), .Res(decalagearidroite_1_res));  // open: C_out
  AandB aandb_1 (.A(A), .B(B), .Res(aandb_1_res));
  AorB aorb_1 (.A(A), .B(B), .Res(aorb_1_res));
  NotA nota_1 (.A(A), .Res(nota_1_res));
  Multiplexer #(.select(3), .width(8)) multiplexer_1 (
    .in0(alusimple8bit_1_res), .in1(alusimple8bit_1_res), .in2(decalagegauche_1_res),
    .in3(decalagedroite_1_res), .in4(decalagearidroite_1_res), .in5(aandb_1_res), .in6(aorb_1_res),
    .in7(nota_1_res), .out(Res), .sel(OP));
  Multiplexer #(.select(3)) multiplexer_2 (
    .in0(alusimple8bit_1_c_out), .in1(alusimple8bit_1_c_out), .in2(decalagegauche_1_c_out),
    .in3(decalagedroite_1_c_out), .in4(1'b0), .in5(1'b0), .in6(1'b0), .in7(1'b0), .out(C_out), .sel(OP));
  Multiplexer #(.select(3)) multiplexer_3 (
    .in0(V_Out_Add_Sub), .in1(1'b0), .in2(V_Out_Decal), .in3(1'b0), .in4(1'b0), .in5(1'b0), .in6(1'b0),
    .in7(1'b0), .out(V_Out), .sel(OP));
  Comparator comparator_1 (.a(Res), .b({8{1'b0}}), .eq(Z_out), .lt(N_out));  // open: gt
endmodule

module DecalageGauche (
  input  [7:0] A,
  output [7:0] Res,
  output C_out,
  output V_out
);

  xor xor_1 (V_out, A[7], A[6]);

  assign C_out = A[7];
  assign Res = {A[6:0], 1'b0};
endmodule

module DecalageDroite (
  input  [7:0] A,
  output [7:0] Res,
  output C_out
);


  assign C_out = A[0];
  assign Res = {1'b0, A[7:1]};
endmodule

module DecalageAriDroite (
  input  [7:0] A,
  output [7:0] Res,
  output C_out
);


  assign C_out = A[0];
  assign Res = {{2{A[7]}}, A[6:1]};
endmodule

module AandB (
  input  [7:0] A,
  input  [7:0] B,
  output [7:0] Res
);

  assign Res = A & B;  // AND_Gate and_1, 8 bits wide
endmodule

module AorB (
  input  [7:0] A,
  input  [7:0] B,
  output [7:0] Res
);

  assign Res = A | B;  // OR_Gate or_1, 8 bits wide
endmodule

module NotA (
  input  [7:0] A,
  output [7:0] Res
);

  assign Res = ~A;  // NOT_Gate not_1, 8 bits wide
endmodule

module ChooseVOut (
  input  [2:0] OP,
  output Sel
);


  assign Sel = OP[1];
endmodule
