// Logisim project Drapeaux.circ as structural Verilog: 17 circuits, main circuit VGA_ctrl
module VGA_ctrl (
  input  [11:0] pixel_in,
  input  clk,
  input  reset,
  output [11:0] pixel,
  output hsync,
  output vsync,
  output [9:0] H_out,
  output [8:0] V_out,
  output frame
);

  wire blank, comparator_1_gt, comparator_2_gt, comparator_3_gt, comparator_4_gt, h_counter_carry, not_1_out,
       not_2_out, v_counter_carry;
  wire [1:0] subtractor_1_out;
  wire [9:0] v_counter_q;
  wire [9:9] subtractor_2_out;
  wire [11:0] h_counter_q, multiplexer_1_out;

  Counter #(.max('hc6a), .width(12)) h_counter (
    .clr(reset), .load(1'b0), .up(1'b1), .count(1'b1), .clk(clk), .D({12{1'b0}}), .carry(h_counter_carry),
    .Q(h_counter_q));
  Counter #(.max('h20d), .width(10)) v_counter (
    .clr(reset), .load(1'b0), .up(1'b1), .count(h_counter_carry), .clk(clk), .carry(v_counter_carry),
    .Q(v_counter_q));  // open: D
  Comparator #(.mode("unsigned"), .width(12)) comparator_1 (
    .a(h_counter_q), .b(12'haee), .gt(comparator_1_gt));  // open: eq, lt
  not not_1 (not_1_out, comparator_1_gt);
  D_Flip_Flop d_ff_1 (.D(not_1_out), .clk(clk), .Q(hsync));  // open: Qn, preset, reset
  // Probe on v_counter_q
  Comparator #(.mode("unsigned"), .width(10)) comparator_2 (
    .a(v_counter_q), .b(10'h20b), .gt(comparator_2_gt));  // open: eq, lt
  D_Flip_Flop d_ff_2 (.D(not_2_out), .clk(clk), .Q(vsync));  // open: Qn, preset, reset
  not not_2 (not_2_out, comparator_2_gt);
  Subtractor #(.width(12)) subtractor_1 (
    .a(h_counter_q), .b(12'h40), .out({H_out, subtractor_1_out}));  // open: bin, bout
  Subtractor #(.width(10)) subtractor_2 (
    .a(v_counter_q), .b(10'h11), .out({subtractor_2_out[9], V_out}));  // open: bin, bout
  and and_1 (frame, v_counter_carry, h_counter_carry);
  Multiplexer #(.width(12)) multiplexer_1 (.in0(pixel_in), .in1({12{1'b0}}), .out(multiplexer_1_out), .sel(blank));
  Comparator #(.mode("unsigned"), .width(12)) comparator_3 (
    .a({H_out, subtractor_1_out}), .b(12'h9ff), .gt(comparator_3_gt));  // open: eq, lt
  Comparator #(.mode("unsigned"), .width(10)) comparator_4 (
    .a({subtractor_2_out[9], V_out}), .b(10'h1df), .gt(comparator_4_gt));  // open: eq, lt
  Register #(.width(12)) register_1 (.D(multiplexer_1_out), .en(1'b1), .clk(clk), .Q(pixel), .clr(reset));
  or or_1 (blank, comparator_3_gt, comparator_4_gt);

  // Other names for the same wires on the sheet: pixel_int[11:0] = pixel_in

  // Notes on the sheet:
  //   vsync: pull=up
  //   pixel: pull=up
  //   hsync: pull=up
  //   Ne pas modifier ce circuit!!!!!
  //   Ne pas modifier ce circuit!!!!!
  //   Contrôle VGA 640 x 480 @ 60 Hz
  //   Ne pas modifier ce circuit!!!!!
endmodule

module Exercise (
  input  [9:0] H_in,
  input  [8:0] V_in,
  input  [3:0] SW_Buttons,
  input  [7:0] SW,
  output [11:0] Pixel
);

  wire [11:0] buttons_1_d_c, congo_1_d_c, france_1_d_f, suede_1_d_s, suisse_1_d_s, tcheque_1_d_t, vaud_1_d_v;

  France france_1 (.H_in(H_in), .D_F(france_1_d_f));
  Vaud vaud_1 (.V_in(V_in), .D_V(vaud_1_d_v));
  Suisse suisse_1 (.H_in(H_in), .V_in(V_in), .D_S(suisse_1_d_s));
  Tcheque tcheque_1 (.V_in(V_in), .H_in(H_in), .D_T(tcheque_1_d_t));
  Suede suede_1 (.H_in(H_in), .V_in(V_in), .D_S(suede_1_d_s));
  Congo congo_1 (.H_in(H_in), .V_in(V_in), .D_C(congo_1_d_c));
  Buttons buttons_1 (.H_in(H_in), .SW(SW_Buttons), .V_in(V_in), .D_C(buttons_1_d_c));
  Multiplexer #(.select(3), .width(12)) multiplexer_1 (
    .in0(france_1_d_f), .in1(vaud_1_d_v), .in2(suisse_1_d_s), .in3(tcheque_1_d_t), .in4(suede_1_d_s),
    .in5(congo_1_d_c), .in6(buttons_1_d_c), .out(Pixel), .sel(SW[2:0]));  // open: in7

  // Notes on the sheet:
  //   Coordonnée horizontale, valeurs entre 0 et 639
  //   Coordonnée verticale, valeurs entre 0 et 479
endmodule

module Image_Gen (
  input  clk,
  input  reset,
  input  [7:0] SW,
  input  [3:0] SW_Buttons,
  output [11:0] pixel,
  output hsync,
  output vsync
);

  wire [8:0] VGA_v_out;
  wire [9:0] VGA_h_out;
  wire [11:0] Drapeaux_pixel;

  VGA_ctrl VGA (
    .pixel_in(Drapeaux_pixel), .clk(clk), .reset(reset), .pixel(pixel), .hsync(hsync), .vsync(vsync),
    .H_out(VGA_h_out), .V_out(VGA_v_out));  // open: frame
  Exercise Drapeaux (.H_in(VGA_h_out), .V_in(VGA_v_out), .SW_Buttons(SW_Buttons), .SW(SW), .Pixel(Drapeaux_pixel));

  // Notes on the sheet:
  //   vsync: pull=up
  //   hsync: pull=up
  //   pixel: pull=up
  //   Ne pas modifier ce circuit!!!!!
  //   Ne pas modifier ce circuit!!!!!
endmodule

module SIM_VGA_ctrl (
  input  rst,
  input  clk,
  output [4:0] H_out,
  output [4:0] V_out,
  output frame,
  output blank
);

  wire h_counter_carry, v_counter_carry;

  Counter #(.max('h1f), .width(5)) h_counter (
    .clr(rst), .load(1'b0), .up(1'b1), .count(1'b1), .clk(clk), .carry(h_counter_carry), .Q(H_out));  // open: D
  Counter #(.max('h1f), .width(5)) v_counter (
    .clr(rst), .load(1'b0), .up(1'b1), .count(h_counter_carry), .clk(clk), .carry(v_counter_carry), .Q(V_out));  // open: D
  Comparator #(.mode("unsigned"), .width(5)) comparator_1 (.a(V_out), .b(5'b10111), .gt(blank));  // open: eq, lt
  and and_1 (frame, v_counter_carry, h_counter_carry);

  // Notes on the sheet:
  //   Ne pas modifier ce circuit!!!!!
endmodule

module SIM_image_Gen (
  input  rst,
  input  clk,
  input  [7:0] Switch,
  input  [3:0] SW_Buttons,
  output [4:0] H_count,
  output [4:0] V_count,
  output [2:0] Pixel
);

  wire sim_vga_ctrl_1_blank;
  wire [3:0] undriven, undriven_2;
  wire [4:0] sim_vscaler_1_out_2;
  wire [5:0] sim_hscaler_1_out_2;
  wire [11:0] exercise_1_pixel;

  SIM_VGA_ctrl sim_vga_ctrl_1 (
    .rst(rst), .clk(clk), .H_out(H_count), .V_out(V_count), .blank(sim_vga_ctrl_1_blank));  // open: frame
  SIM_hscaler sim_hscaler_1 (.in_1(H_count), .out_2(sim_hscaler_1_out_2));
  SIM_vscaler sim_vscaler_1 (.in_1(V_count), .out_2(sim_vscaler_1_out_2));
  Exercise exercise_1 (
    .H_in({sim_hscaler_1_out_2, undriven_2}), .V_in({sim_vscaler_1_out_2, undriven}),
    .SW_Buttons(SW_Buttons), .SW(Switch), .Pixel(exercise_1_pixel));
  Multiplexer #(.width(3)) multiplexer_1 (
    .in0({exercise_1_pixel[11], exercise_1_pixel[7], exercise_1_pixel[3]}), .in1(3'b000), .out(Pixel),
    .sel(sim_vga_ctrl_1_blank));

  // Notes on the sheet:
  //   Ne pas modifier ce circuit!!!!!
  //   Ne pas modifier ce circuit!!!!!
endmodule

module SIM_console (
  input  reset,
  input  [7:0] Switch,
  input  [3:0] in_3
);

  wire clk_out;
  wire [2:0] rgb_video_1_p6;
  wire [4:0] rgb_video_1_p4, rgb_video_1_p5;

  Clock clk (.out(clk_out));
  // RGB_Video #(.height(32), .reset("Synchronous"), .scale(8), .width(32)) rgb_video_1: pin names not known; wires that end beside it: reset, clk_out, 1'b1, rgb_video_1_p4, rgb_video_1_p5, rgb_video_1_p6
  SIM_image_Gen sim_image_gen_1 (
    .rst(reset), .clk(clk_out), .Switch(Switch), .SW_Buttons(in_3), .H_count(rgb_video_1_p4),
    .V_count(rgb_video_1_p5), .Pixel(rgb_video_1_p6));

  // Notes on the sheet:
  //   Ne pas modifier ce circuit!!!!!
  //   Ne pas modifier ce circuit!!!!!
endmodule

module SIM_hscaler (
  input  [4:0] in_1,
  output [5:0] out_2
);

  wire [6:0] bit_extender_1_out, multiplier_1_out;
  wire [6:6] divider_1_out;

  assign bit_extender_1_out = {{2{1'b0}}, in_1};  // Bit_Extender bit_extender_1
  Multiplier #(.width(7)) multiplier_1 (
    .a(bit_extender_1_out), .b(7'b0000100), .out(multiplier_1_out));  // open: cin, cout
  Divider #(.width(7)) divider_1 (
    .a(multiplier_1_out), .b(7'b0000011), .out({divider_1_out[6], out_2}));  // open: upper, rem

  // Notes on the sheet:
  //   Ne pas modifier ce circuit!!!!!
endmodule

module SIM_vscaler (
  input  [4:0] in_1,
  output [4:0] out_2
);

  wire [6:0] bit_extender_1_out, multiplier_1_out;
  wire [6:5] divider_1_out;

  assign bit_extender_1_out = {{2{1'b0}}, in_1};  // Bit_Extender bit_extender_1
  Multiplier #(.width(7)) multiplier_1 (
    .a(bit_extender_1_out), .b(7'b0000100), .out(multiplier_1_out));  // open: cin, cout
  Divider #(.width(7)) divider_1 (
    .a(multiplier_1_out), .b(7'b0000011), .out({divider_1_out, out_2}));  // open: upper, rem

  // Notes on the sheet:
  //   Ne pas modifier ce circuit!!!!!
endmodule

module France (
  input  [9:0] H_in,
  output [11:0] D_F
);

  wire comparator_1_gt, comparator_2_lt;
  wire [11:0] multiplexer_1_out;

  Comparator #(.mode("unsigned"), .width(10)) comparator_1 (
    .a(H_in), .b(10'h1aa), .gt(comparator_1_gt));  // open: eq, lt
  Comparator #(.mode("unsigned"), .width(10)) comparator_2 (
    .a(H_in), .b(10'hd5), .lt(comparator_2_lt));  // open: gt, eq
  Multiplexer #(.width(12)) multiplexer_1 (
    .in0({12{1'b1}}), .in1(12'hf), .out(multiplexer_1_out), .sel(comparator_2_lt));
  Multiplexer #(.width(12)) multiplexer_2 (.in0(multiplexer_1_out), .in1(12'hf00), .out(D_F), .sel(comparator_1_gt));
endmodule

module Vaud (
  input  [8:0] V_in,
  output [11:0] D_V
);

  wire comparator_1_gt;

  Comparator #(.mode("unsigned"), .width(9)) comparator_1 (.a(V_in), .b(9'hef), .gt(comparator_1_gt));  // open: eq, lt
  Multiplexer #(.width(12)) multiplexer_1 (.in0({12{1'b1}}), .in1(12'hf0), .out(D_V), .sel(comparator_1_gt));
endmodule

module Suisse (
  input  [9:0] H_in,
  input  [8:0] V_in,
  output [11:0] D_S
);

  wire and_1_out, and_2_out, and_3_out, and_4_out, and_5_out, and_6_out, comparator_1_gt, comparator_2_lt,
       comparator_3_gt, comparator_4_lt, comparator_5_gt, comparator_6_lt, comparator_7_gt, comparator_8_lt,
       comparator_9_gt, or_1_out;
  wire [11:0] multiplexer_1_out;

  Comparator #(.mode("unsigned"), .width(9)) comparator_1 (.a(V_in), .b(9'h5a), .gt(comparator_1_gt));  // open: eq, lt
  Comparator #(.mode("unsigned"), .width(9)) comparator_2 (.a(V_in), .b(9'h186), .lt(comparator_2_lt));  // open: gt, eq
  Comparator #(.mode("unsigned"), .width(10)) comparator_3 (
    .a(H_in), .b(10'hc3), .gt(comparator_3_gt));  // open: eq, lt
  Comparator #(.mode("unsigned"), .width(10)) comparator_4 (
    .a(H_in), .b(10'h11d), .lt(comparator_4_lt));  // open: gt, eq
  Comparator #(.mode("unsigned"), .width(9)) comparator_5 (.a(V_in), .b(9'hc3), .gt(comparator_5_gt));  // open: eq, lt
  Comparator #(.mode("unsigned"), .width(9)) comparator_6 (.a(V_in), .b(9'h11d), .lt(comparator_6_lt));  // open: gt, eq
  Comparator #(.mode("unsigned"), .width(10)) comparator_7 (
    .a(H_in), .b(10'h5a), .gt(comparator_7_gt));  // open: eq, lt
  Comparator #(.mode("unsigned"), .width(10)) comparator_8 (
    .a(H_in), .b(10'h186), .lt(comparator_8_lt));  // open: gt, eq
  and and_1 (and_1_out, comparator_1_gt, comparator_2_lt);
  and and_2 (and_2_out, comparator_3_gt, comparator_4_lt);
  and and_3 (and_3_out, comparator_5_gt, comparator_6_lt);
  and and_4 (and_4_out, comparator_7_gt, comparator_8_lt);
  and and_5 (and_5_out, and_1_out, and_2_out);
  and and_6 (and_6_out, and_3_out, and_4_out);
  Comparator #(.mode("unsigned"), .width(10)) comparator_9 (
    .a(H_in), .b(10'h1f1), .gt(comparator_9_gt));  // open: eq, lt
  Multiplexer #(.width(12)) multiplexer_1 (.in0(12'hf00), .in1({12{1'b1}}), .out(multiplexer_1_out), .sel(or_1_out));
  or or_1 (or_1_out, and_5_out, and_6_out);
  Multiplexer #(.width(12)) multiplexer_2 (.in0(multiplexer_1_out), .in1({12{1'b0}}), .out(D_S), .sel(comparator_9_gt));
endmodule

module Tcheque (
  input  [8:0] V_in,
  input  [9:0] H_in,
  output [11:0] D_T
);

  wire and_1_out, comparator_1_gt, comparator_2_gt, comparator_3_gt;
  wire [9:0] nine_to_ten_1_ten, subtractor_1_out;
  wire [11:0] multiplexer_1_out;

  Nine_to_Ten nine_to_ten_1 (.V_in(V_in), .Ten(nine_to_ten_1_ten));
  Subtractor #(.width(10)) subtractor_1 (
    .a(10'h1e0), .b(nine_to_ten_1_ten), .out(subtractor_1_out));  // open: bin, bout
  Comparator #(.mode("unsigned"), .width(10)) comparator_1 (
    .a(nine_to_ten_1_ten), .b(H_in), .gt(comparator_1_gt));  // open: eq, lt
  Comparator #(.mode("unsigned"), .width(10)) comparator_2 (
    .a(subtractor_1_out), .b(H_in), .gt(comparator_2_gt));  // open: eq, lt
  and and_1 (and_1_out, comparator_1_gt, comparator_2_gt);
  Comparator #(.width(10)) comparator_3 (.a(nine_to_ten_1_ten), .b(10'hf0), .gt(comparator_3_gt));  // open: eq, lt
  Multiplexer #(.width(12)) multiplexer_1 (
    .in0({12{1'b1}}), .in1(12'hf00), .out(multiplexer_1_out), .sel(comparator_3_gt));
  Multiplexer #(.width(12)) multiplexer_2 (.in0(multiplexer_1_out), .in1(12'hf), .out(D_T), .sel(and_1_out));
endmodule

module Nine_to_Ten (
  input  [8:0] V_in,
  output [9:0] Ten
);


  assign Ten = {1'b0, V_in};
endmodule

module Suede (
  input  [9:0] H_in,
  input  [8:0] V_in,
  output [11:0] D_S
);

  wire and_1_out, and_2_out, comparator_1_gt, comparator_2_lt, comparator_3_gt, comparator_4_lt, or_1_out;

  Comparator #(.mode("unsigned"), .width(10)) comparator_1 (
    .a(H_in), .b(10'hc8), .gt(comparator_1_gt));  // open: eq, lt
  Comparator #(.mode("unsigned"), .width(10)) comparator_2 (
    .a(H_in), .b(10'h118), .lt(comparator_2_lt));  // open: gt, eq
  Comparator #(.mode("unsigned"), .width(9)) comparator_3 (.a(V_in), .b(9'hc0), .gt(comparator_3_gt));  // open: eq, lt
  Comparator #(.mode("unsigned"), .width(9)) comparator_4 (.a(V_in), .b(9'h120), .lt(comparator_4_lt));  // open: gt, eq
  and and_1 (and_1_out, comparator_1_gt, comparator_2_lt);
  and and_2 (and_2_out, comparator_3_gt, comparator_4_lt);
  or or_1 (or_1_out, and_1_out, and_2_out);
  Multiplexer #(.width(12)) multiplexer_1 (.in0(12'hf), .in1(12'hff0), .out(D_S), .sel(or_1_out));
endmodule

module Congo (
  input  [9:0] H_in,
  input  [8:0] V_in,
  output [11:0] D_C
);

  wire comparator_1_lt, comparator_2_lt;
  wire [9:0] nine_to_ten_1_ten, subtractor_1_out, subtractor_2_out;
  wire [11:0] multiplexer_1_out;

  Subtractor #(.width(10)) subtractor_1 (
    .a(10'h1e0), .b(nine_to_ten_1_ten), .out(subtractor_1_out));  // open: bin, bout
  Subtractor #(.width(10)) subtractor_2 (
    .a(10'h280), .b(nine_to_ten_1_ten), .out(subtractor_2_out));  // open: bin, bout
  Comparator #(.mode("unsigned"), .width(10)) comparator_1 (
    .a(H_in), .b(subtractor_1_out), .lt(comparator_1_lt));  // open: gt, eq
  Comparator #(.mode("unsigned"), .width(10)) comparator_2 (
    .a(H_in), .b(subtractor_2_out), .lt(comparator_2_lt));  // open: gt, eq
  Nine_to_Ten nine_to_ten_1 (.V_in(V_in), .Ten(nine_to_ten_1_ten));
  Multiplexer #(.width(12)) multiplexer_1 (.in0(12'hff0), .in1(12'hf0), .out(multiplexer_1_out), .sel(comparator_1_lt));
  Multiplexer #(.width(12)) multiplexer_2 (.in0(12'hf00), .in1(multiplexer_1_out), .out(D_C), .sel(comparator_2_lt));
endmodule

module Carre (
  input  [9:0] H_in,
  input  [9:0] Start_h,
  input  SW,
  input  [9:0] Stop_h,
  input  [8:0] V_in,
  input  [8:0] Start_v,
  input  [8:0] Stop_v,
  output [11:0] pixel
);

  wire and_1_out, and_2_out, and_3_out, comparator_1_gt, comparator_2_lt, comparator_3_gt, comparator_4_lt;
  wire [11:0] multiplexer_1_out;

  Comparator #(.mode("unsigned"), .width(10)) comparator_1 (
    .a(H_in), .b(Start_h), .gt(comparator_1_gt));  // open: eq, lt
  Comparator #(.mode("unsigned"), .width(10)) comparator_2 (
    .a(H_in), .b(Stop_h), .lt(comparator_2_lt));  // open: gt, eq
  Comparator #(.mode("unsigned"), .width(9)) comparator_3 (
    .a(V_in), .b(Start_v), .gt(comparator_3_gt));  // open: eq, lt
  Comparator #(.mode("unsigned"), .width(9)) comparator_4 (.a(V_in), .b(Stop_v), .lt(comparator_4_lt));  // open: gt, eq
  and and_1 (and_1_out, comparator_1_gt, comparator_2_lt);
  and and_2 (and_2_out, comparator_3_gt, comparator_4_lt);
  Multiplexer #(.width(12)) multiplexer_1 (.in0(12'hff0), .in1(12'hf), .out(multiplexer_1_out), .sel(SW));
  and and_3 (and_3_out, and_1_out, and_2_out);
  Multiplexer #(.width(12)) multiplexer_2 (.in0(12'h666), .in1(multiplexer_1_out), .out(pixel), .sel(and_3_out));
endmodule

module Buttons (
  input  [9:0] H_in,
  input  [3:0] SW,
  input  [8:0] V_in,
  output [11:0] D_C
);

  wire [11:0] carre_1_pixel, carre_2_pixel, carre_3_pixel, carre_4_pixel;

  Carre carre_1 (
    .H_in(H_in), .Start_h(10'h3c), .SW(SW[3]), .Stop_h(10'h8c), .V_in(V_in), .Start_v(9'ha0),
    .Stop_v(9'h140), .pixel(carre_1_pixel));
  Carre carre_2 (
    .H_in(H_in), .Start_h(10'hc8), .SW(SW[2]), .Stop_h(10'h118), .V_in(V_in), .Start_v(9'ha0),
    .Stop_v(9'h140), .pixel(carre_2_pixel));
  Carre carre_3 (
    .H_in(H_in), .Start_h(10'h154), .SW(SW[1]), .Stop_h(10'h1a4), .V_in(V_in), .Start_v(9'ha0),
    .Stop_v(9'h140), .pixel(carre_3_pixel));
  Carre carre_4 (
    .H_in(H_in), .Start_h(10'h1e0), .SW(SW[0]), .Stop_h(10'h230), .V_in(V_in), .Start_v(9'ha0),
    .Stop_v(9'h140), .pixel(carre_4_pixel));
  assign D_C = carre_1_pixel | carre_2_pixel | carre_3_pixel | carre_4_pixel;  // OR_Gate or_1, 12 bits wide
endmodule
