// Logisim project Labo2.circ as structural Verilog
module main (
  input  A1,
  input  A2,
  input  B1,
  input  B2,
  output L1,
  output L2
);

  wire and_1_out, and_2_out, and_3_out, and_4_out, and_5_out, and_6_out, not_1_out, not_2_out, not_3_out,
       not_4_out;

  not not_1 (not_1_out, A1);
  not not_2 (not_2_out, A2);
  not not_3 (not_3_out, B1);
  not not_4 (not_4_out, B2);
  and and_1 (and_1_out, A2, not_3_out, B2);
  and and_2 (and_2_out, not_1_out, A2, B1, not_4_out);
  and and_3 (and_3_out, A1, not_2_out, B1, B2);
  and and_4 (and_4_out, not_1_out, A2, B2);
  and and_5 (and_5_out, A1, not_2_out, not_3_out, B2);
  and and_6 (and_6_out, A1, A2, B1, not_4_out);
  or or_1 (L1, and_1_out, and_2_out, and_3_out);
  or or_2 (L2, and_4_out, and_5_out, and_6_out);
endmodule

module Seg_7 (
  input  A1,
  input  A2,
  input  B1,
  input  B2,
  output Seg1,
  output Seg2,
  output Seg3,
  output Seg4,
  output Seg5,
  output Seg6,
  output Seg7
);

  wire and_1_out, and_2_out, and_3_out, and_4_out, and_5_out, and_6_out, and_7_out, and_8_out, and_9_out,
       and_10_out, and_11_out, and_12_out, and_13_out, and_14_out, and_15_out, and_16_out, and_17_out,
       and_18_out, and_19_out, and_20_out, and_21_out, and_22_out, and_23_out, and_24_out, not_1_out,
       not_2_out, not_3_out, not_4_out;

  not not_1 (not_1_out, A1);
  not not_2 (not_2_out, A2);
  not not_3 (not_3_out, B1);
  not not_4 (not_4_out, B2);
  and and_1 (and_1_out, A2, B2);
  and and_2 (and_2_out, A2, B1);
  and and_3 (and_3_out, A1, B2);
  and and_4 (and_4_out, A1, B1);
  and and_5 (and_5_out, not_1_out, A2, B1);
  and and_6 (and_6_out, A1, not_2_out, B2);
  and and_7 (and_7_out, A1, not_3_out, B2);
  and and_8 (and_8_out, A2, B1, not_4_out);
  and and_9 (and_9_out, not_1_out, A2, B1);
  and and_10 (and_10_out, A1, not_2_out, B2);
  and and_11 (and_11_out, A1, not_3_out, B2);
  and and_12 (and_12_out, A2, B1, not_4_out);
  and and_13 (and_13_out, not_1_out, A2, B2);
  and and_14 (and_14_out, A1, not_2_out, not_3_out, B2);
  and and_15 (and_15_out, A1, B1, not_4_out);
  and and_16 (and_16_out, A2, B1, B2);
  and and_17 (and_17_out, A2, B2);
  and and_18 (and_18_out, A2, B1);
  and and_19 (and_19_out, A1, B2);
  and and_20 (and_20_out, A1, B1);
  and and_21 (and_21_out, A2, B2);
  and and_22 (and_22_out, A2, B1);
  and and_23 (and_23_out, A1, B2);
  and and_24 (and_24_out, A1, B1);
  or or_1 (Seg1, and_1_out, and_2_out, and_3_out, and_4_out);
  or or_2 (Seg2, and_5_out, and_6_out, and_7_out, and_8_out);
  or or_3 (Seg3, and_9_out, and_10_out, and_11_out, and_12_out);
  or or_4 (Seg4, and_13_out, and_14_out, and_15_out, and_16_out);
  or or_5 (Seg5, and_17_out, and_18_out, and_19_out, and_20_out);
  or or_6 (Seg6, and_21_out, and_22_out, and_23_out, and_24_out);
  _7_Segment_Display u_7_segment_display_1 (
    .g(1'b1), .f(Seg6), .a(Seg1), .b(Seg2), .e(Seg5), .d(Seg4), .c(Seg3));  // open: dp

  assign Seg7 = 1'b1;
endmodule

module Bin_To_7 (
  input  B4,
  input  B3,
  input  B2,
  input  B1,
  output Seg1,
  output Seg2,
  output Seg3,
  output Seg4,
  output Seg5,
  output Seg6,
  output Seg7
);

  wire and_1_out, and_2_out, and_3_out, and_4_out, and_5_out, and_6_out, and_7_out, and_8_out, and_9_out,
       and_10_out, and_11_out, and_12_out, and_13_out, and_14_out, and_15_out, and_16_out, and_17_out,
       and_18_out, and_19_out, and_20_out, and_21_out, and_22_out, and_23_out, and_24_out, and_25_out,
       and_26_out, and_27_out, and_28_out, and_29_out, and_30_out, and_31_out, and_32_out, and_33_out,
       and_34_out, and_35_out, and_36_out, and_37_out, and_38_out, and_39_out, and_40_out, not_1_out,
       not_2_out, not_3_out, not_4_out;

  not not_1 (not_1_out, B4);
  not not_2 (not_2_out, B3);
  not not_3 (not_3_out, B2);
  not not_4 (not_4_out, B1);
  and and_1 (and_1_out, not_2_out, not_4_out);
  and and_2 (and_2_out, not_1_out, B2);
  and and_3 (and_3_out, not_1_out, B3, B1);
  and and_4 (and_4_out, B4, not_2_out, not_3_out);
  and and_5 (and_5_out, B4, not_4_out);
  and and_6 (and_6_out, B3, B2);
  and and_7 (and_7_out, not_1_out, not_3_out, not_4_out);
  and and_8 (and_8_out, not_1_out, B2, B1);
  and and_9 (and_9_out, not_2_out, not_4_out);
  and and_10 (and_10_out, B4, not_3_out, B1);
  and and_11 (and_11_out, not_1_out, not_2_out);
  and and_12 (and_12_out, not_1_out, B3);
  and and_13 (and_13_out, B4, not_2_out);
  and and_14 (and_14_out, not_3_out, B1);
  and and_15 (and_15_out, not_1_out, not_3_out);
  and and_16 (and_16_out, not_1_out, B1);
  and and_17 (and_17_out, B3, not_3_out, B1);
  and and_18 (and_18_out, not_1_out, not_2_out, not_4_out);
  and and_19 (and_19_out, not_1_out, not_2_out, B2);
  and and_20 (and_20_out, not_1_out, B2, not_4_out);
  and and_21 (and_21_out, not_2_out, not_3_out, not_4_out);
  and and_22 (and_22_out, B4, not_2_out, B1);
  and and_23 (and_23_out, B4, not_3_out);
  and and_24 (and_24_out, B3, B2, not_4_out);
  and and_25 (and_25_out, not_2_out, not_4_out);
  and and_26 (and_26_out, B2, not_4_out);
  and and_27 (and_27_out, B4, B2);
  and and_28 (and_28_out, B4, B3);
  and and_29 (and_29_out, not_3_out, not_4_out);
  and and_30 (and_30_out, not_1_out, B3, not_3_out);
  and and_31 (and_31_out, B3, not_4_out);
  and and_32 (and_32_out, B4, not_2_out);
  and and_33 (and_33_out, B4, B2);
  and and_34 (and_34_out, not_2_out, B2);
  and and_35 (and_35_out, B4, not_2_out);
  and and_36 (and_36_out, not_1_out, B3, not_3_out);
  and and_37 (and_37_out, not_1_out, B3, not_4_out);
  and and_38 (and_38_out, B3, not_3_out, B1);
  and and_39 (and_39_out, B2, not_4_out);
  and and_40 (and_40_out, B4, B1);
  or or_1 (Seg1, and_1_out, and_2_out, and_3_out, and_4_out, and_5_out, and_6_out);
  or or_2 (Seg2, and_7_out, and_8_out, and_9_out, and_10_out, and_11_out);
  or or_3 (Seg3, and_12_out, and_13_out, and_14_out, and_15_out, and_16_out);
  or or_4 (Seg4, and_17_out, and_18_out, and_19_out, and_20_out, and_21_out, and_22_out, and_23_out, and_24_out);
  or or_5 (Seg5, and_25_out, and_26_out, and_27_out, and_28_out);
  or or_6 (Seg6, and_29_out, and_30_out, and_31_out, and_32_out, and_33_out);
  or or_7 (Seg7, and_34_out, and_35_out, and_36_out, and_37_out, and_38_out, and_39_out, and_40_out);
  _7_Segment_Display u_7_segment_display_1 (
    .g(Seg7), .f(Seg6), .a(Seg1), .b(Seg2), .e(Seg5), .d(Seg4), .c(Seg3));  // open: dp
endmodule

module Add1Bit (
  input  A,
  input  B,
  input  C,
  output Res,
  output C_out
);

  wire and_1_out, and_2_out, and_3_out, xor_1_out;

  xor xor_1 (xor_1_out, A, B);
  and and_1 (and_1_out, A, B);
  and and_2 (and_2_out, A, C);
  and and_3 (and_3_out, B, C);
  xor xor_2 (Res, xor_1_out, C);
  or or_1 (C_out, and_1_out, and_2_out, and_3_out);
endmodule

module Add4Bit (
  input  [3:0] A,
  input  C,
  input  [3:0] B,
  output [3:0] Res,
  output C_Out
);

  wire add1bit_1_c_out, add1bit_2_c_out, add1bit_3_c_out;

  Add1Bit add1bit_1 (.A(A[0]), .B(B[0]), .C(C), .Res(Res[0]), .C_out(add1bit_1_c_out));
  Add1Bit add1bit_2 (.A(A[1]), .B(B[1]), .C(add1bit_1_c_out), .Res(Res[1]), .C_out(add1bit_2_c_out));
  Add1Bit add1bit_3 (.A(A[2]), .B(B[2]), .C(add1bit_2_c_out), .Res(Res[2]), .C_out(add1bit_3_c_out));
  Add1Bit add1bit_4 (.A(A[3]), .B(B[3]), .C(add1bit_3_c_out), .Res(Res[3]), .C_out(C_Out));
endmodule

module Add4Bit_7 (
  input  [3:0] A,
  input  C,
  input  [3:0] B,
  output C_Out
);

  wire bin_to_7_1_seg1, bin_to_7_1_seg2, bin_to_7_1_seg3, bin_to_7_1_seg4, bin_to_7_1_seg5, bin_to_7_1_seg6,
       bin_to_7_1_seg7;
  wire [3:0] add4bit_1_res;

  Add4Bit add4bit_1 (.A(A), .C(C), .B(B), .Res(add4bit_1_res), .C_Out(C_Out));
  Bin_To_7 bin_to_7_1 (
    .B4(add4bit_1_res[3]), .B3(add4bit_1_res[2]), .B2(add4bit_1_res[1]), .B1(add4bit_1_res[0]),
    .Seg1(bin_to_7_1_seg1), .Seg2(bin_to_7_1_seg2), .Seg3(bin_to_7_1_seg3), .Seg4(bin_to_7_1_seg4),
    .Seg5(bin_to_7_1_seg5), .Seg6(bin_to_7_1_seg6), .Seg7(bin_to_7_1_seg7));
  _7_Segment_Display u_7_segment_display_1 (
    .g(bin_to_7_1_seg7), .f(bin_to_7_1_seg6), .a(bin_to_7_1_seg1), .b(bin_to_7_1_seg2), .e(bin_to_7_1_seg5),
    .d(bin_to_7_1_seg4), .c(bin_to_7_1_seg3));  // open: dp
endmodule

module Hamming_Cod (
  input  D3,
  input  D2,
  input  D1,
  input  D0,
  output H6,
  output H5,
  output H4,
  output H3,
  output H2,
  output H1,
  output H0
);

  wire and_1_out, and_2_out, and_3_out, and_4_out, and_5_out, and_6_out, and_7_out, and_8_out, and_9_out,
       and_10_out, and_11_out, and_12_out, not_1_out, not_2_out, not_3_out, not_4_out;

  not not_1 (not_1_out, D3);
  not not_2 (not_2_out, D2);
  not not_3 (not_3_out, D1);
  not not_4 (not_4_out, D0);
  and and_1 (and_1_out, not_1_out, not_2_out, D1);
  and and_2 (and_2_out, not_1_out, D2, not_3_out);
  and and_3 (and_3_out, D3, not_2_out, not_3_out);
  and and_4 (and_4_out, D3, D2, D1);
  and and_5 (and_5_out, not_2_out, not_3_out, D0);
  and and_6 (and_6_out, not_2_out, D1, not_4_out);
  and and_7 (and_7_out, D2, not_3_out, not_4_out);
  and and_8 (and_8_out, D2, D1, D0);
  and and_9 (and_9_out, D3, not_3_out, not_4_out);
  and and_10 (and_10_out, D3, D1, D0);
  and and_11 (and_11_out, not_1_out, not_3_out, D0);
  and and_12 (and_12_out, not_1_out, D1, not_4_out);
  or or_1 (H2, and_1_out, and_2_out, and_3_out, and_4_out);
  or or_2 (H1, and_5_out, and_6_out, and_7_out, and_8_out);
  or or_3 (H0, and_9_out, and_10_out, and_11_out, and_12_out);

  assign H3 = D0;
  assign H4 = D1;
  assign H5 = D2;
  assign H6 = D3;
endmodule

module FCS_VHDL_Seg7 (
  input  A1,
  input  A2,
  input  B1,
  input  B2
);

  wire fcs_1_s1, fcs_1_s2, fcs_1_s3, fcs_1_s4, fcs_1_s5, fcs_1_s6, fcs_1_s7, main_1_l1, main_1_l2;

  main main_1 (.A1(A1), .A2(A2), .B1(B1), .B2(B2), .L1(main_1_l1), .L2(main_1_l2));
  FCS fcs_1 (
    .l1(main_1_l1), .l2(main_1_l2), .s1(fcs_1_s1), .s2(fcs_1_s2), .s3(fcs_1_s3), .s4(fcs_1_s4),
    .s5(fcs_1_s5), .s6(fcs_1_s6), .s7(fcs_1_s7));
  _7_Segment_Display u_7_segment_display_1 (
    .g(fcs_1_s7), .f(fcs_1_s6), .a(fcs_1_s1), .b(fcs_1_s2), .e(fcs_1_s5), .d(fcs_1_s4), .c(fcs_1_s3));  // open: dp
endmodule

module Majorite (
  input  a,
  input  b,
  input  c,
  output MAJ
);

  wire and_1_out, and_2_out, and_3_out;

  and and_1 (and_1_out, b, c);
  and and_2 (and_2_out, a, c);
  or or_1 (MAJ, and_1_out, and_2_out, and_3_out);
  and and_3 (and_3_out, a, b);
endmodule

// VHDL entity FCS, as the project stores it:
--------------------------------------------------------------------------------
-- Project :
-- File    :
-- Autor   :
-- Date    :
--
--------------------------------------------------------------------------------
-- Description :
--
--------------------------------------------------------------------------------

LIBRARY ieee;
USE ieee.std_logic_1164.all;

ENTITY FCS IS
  PORT (
  ------------------------------------------------------------------------------
    l1		: IN  std_logic;
    l2		: IN  std_logic;
  ------------------------------------------------------------------------------
    s1		: OUT std_logic;
    s2		: OUT std_logic;
    s3		: OUT std_logic;
    s4		: OUT std_logic;
    s5		: OUT std_logic;
    s6		: OUT std_logic;
    s7		: OUT std_logic
    );
END FCS;

--------------------------------------------------------------------------------
--Complete your VHDL description below
--------------------------------------------------------------------------------

ARCHITECTURE TypeArchitecture OF FCS IS

BEGIN
	s1 <= (l1 xor l2) or (l1 and l2);
	s2 <= (l1 xor l2);
	s3 <= (l1 xor l2);
	s4 <= l2 and (not l1);
	s5 <= (l1 xor l2) or (l1 and l2);
	s6 <= (l1 xor l2) or (l1 and l2);
	s7 <= '1';

END TypeArchitecture;
