// Logisim project Labos.circ as structural Verilog: 6 circuits, main circuit Add8Bit
module Add1Bit (
  input  a,
  input  b,
  input  c_in,
  output Res,
  output c_out
);

  wire and_1_out, and_2_out, and_3_out, and_4_out, or_1_out, xnor_1_out, xor_1_out;

  xnor xnor_1 (xnor_1_out, a, b);
  xor xor_1 (xor_1_out, b, a);
  or or_1 (or_1_out, b, c_in);
  and and_1 (and_1_out, xnor_1_out, c_in);
  and and_2 (and_2_out, xor_1_out, ~c_in);  // AND_Gate
  and and_3 (and_3_out, or_1_out, a);
  and and_4 (and_4_out, b, c_in);
  or or_2 (Res, and_1_out, and_2_out);
  or or_3 (c_out, and_3_out, and_4_out);
endmodule

// Add1Bit1
module Add2Bit (
  input  a0,
  input  a1,
  input  c_in,
  input  b0,
  input  b1,
  output Res0,
  output Res1,
  output c_out
);

  wire Add1Bit0_c_out;

  Add1Bit Add1Bit0 (.a(a0), .b(b0), .c_in(c_in), .Res(Res0), .c_out(Add1Bit0_c_out));
  Add1Bit Add1Bit1 (.a(a1), .b(b1), .c_in(Add1Bit0_c_out), .Res(Res1), .c_out(c_out));
endmodule

module Add4Bit (
  input  a0,
  input  a1,
  input  a2,
  input  a3,
  input  c_in,
  input  b0,
  input  b1,
  input  b2,
  input  b3,
  output R0,
  output R1,
  output R2,
  output R3,
  output c_out
);

  wire Add2Bit01_c_out;

  Add2Bit Add2Bit01 (.a0(a0), .a1(a1), .c_in(c_in), .b0(b0), .b1(b1), .Res0(R0), .Res1(R1), .c_out(Add2Bit01_c_out));
  Add2Bit Add2Bit23 (.a0(a2), .a1(a3), .c_in(Add2Bit01_c_out), .b0(b2), .b1(b3), .Res0(R2), .Res1(R3), .c_out(c_out));
endmodule

module Add8Bit (
  input  c_in,
  input  a0,
  input  a1,
  input  a2,
  input  a3,
  input  b0,
  input  b1,
  input  b2,
  input  b3,
  input  a4,
  input  a5,
  input  a6,
  input  a7,
  input  b4,
  input  b5,
  input  b6,
  input  b7,
  output R0,
  output R1,
  output R2,
  output R3,
  output R4,
  output R5,
  output R6,
  output R7,
  output c_out
);

  wire AddBit0123_c_out;

  Add4Bit AddBit0123 (
    .a0(a0), .a1(a1), .a2(a2), .a3(a3), .c_in(c_in), .b0(b0), .b1(b1), .b2(b2), .b3(b3), .R0(R0), .R1(R1),
    .R2(R2), .R3(R3), .c_out(AddBit0123_c_out));
  Add4Bit AddBit4567 (
    .a0(a4), .a1(a5), .a2(a6), .a3(a7), .c_in(AddBit0123_c_out), .b0(b4), .b1(b5), .b2(b6), .b3(b7), .R0(R4),
    .R1(R5), .R2(R6), .R3(R7), .c_out(c_out));
endmodule

module FCS (
  input  J11,
  input  J10,
  input  J21,
  input  J20,
  output L1,
  output L2
);

  wire and_1_out, and_2_out, and_3_out, and_4_out, and_5_out, and_6_out, and_7_out, and_8_out, not_1_out,
       not_2_out, not_3_out, not_4_out;

  not not_1 (not_1_out, J11);
  not not_2 (not_2_out, J10);
  not not_3 (not_3_out, J21);
  not not_4 (not_4_out, J20);
  and and_1 (and_1_out, J10, not_3_out, J20);
  and and_2 (and_2_out, not_1_out, J10, J21, not_4_out);
  and and_3 (and_3_out, J11, not_2_out, J21);
  and and_4 (and_4_out, J11, J10, J20);
  and and_5 (and_5_out, not_1_out, J10, J20);
  and and_6 (and_6_out, J11, not_2_out, not_3_out, J20);
  and and_7 (and_7_out, J11, J21, not_4_out);
  and and_8 (and_8_out, J11, J10, J21);
  or or_1 (L1, and_1_out, and_2_out, and_3_out, and_4_out);
  or or_2 (L2, and_5_out, and_6_out, and_7_out, and_8_out);
endmodule

module Dec_7 (
  input  a,
  input  b,
  input  c,
  input  d,
  output seg1,
  output seg2,
  output seg3,
  output seg4,
  output seg5,
  output seg6,
  output seg7
);

  wire and_1_out, and_2_out, and_3_out, and_4_out, and_5_out, and_6_out, and_7_out, and_8_out, and_9_out,
       and_10_out, and_11_out, and_12_out, and_13_out, and_14_out, and_15_out, and_16_out, and_17_out,
       and_18_out, and_19_out, and_20_out, and_21_out, and_22_out, and_23_out, and_24_out, and_25_out,
       and_26_out, and_27_out, and_28_out, and_29_out, and_30_out, and_31_out, and_32_out, and_33_out,
       and_34_out, and_35_out, and_36_out, and_37_out, and_38_out, and_39_out, and_40_out, not_1_out,
       not_2_out, not_3_out, not_4_out;

  not not_1 (not_1_out, a);
  not not_2 (not_2_out, b);
  not not_3 (not_3_out, c);
  not not_4 (not_4_out, d);
  and and_1 (and_1_out, not_2_out, not_4_out);
  and and_2 (and_2_out, not_1_out, c);
  and and_3 (and_3_out, not_1_out, b, d);
  and and_4 (and_4_out, a, not_2_out, not_3_out);
  and and_5 (and_5_out, a, not_4_out);
  and and_6 (and_6_out, b, c);
  and and_7 (and_7_out, not_1_out, not_3_out, not_4_out);
  and and_8 (and_8_out, not_1_out, c, d);
  and and_9 (and_9_out, not_2_out, not_4_out);
  and and_10 (and_10_out, a, not_3_out, d);
  and and_11 (and_11_out, not_1_out, not_2_out);
  and and_12 (and_12_out, not_1_out, b);
  and and_13 (and_13_out, a, not_2_out);
  and and_14 (and_14_out, not_3_out, d);
  and and_15 (and_15_out, not_1_out, not_3_out);
  and and_16 (and_16_out, not_1_out, d);
  and and_17 (and_17_out, b, not_3_out, d);
  and and_18 (and_18_out, not_1_out, not_2_out, not_4_out);
  and and_19 (and_19_out, not_1_out, not_2_out, c);
  and and_20 (and_20_out, not_1_out, c, not_4_out);
  and and_21 (and_21_out, not_2_out, not_3_out, not_4_out);
  and and_22 (and_22_out, a, not_3_out);
  and and_23 (and_23_out, not_2_out, c, d);
  and and_24 (and_24_out, b, c, not_4_out);
  and and_25 (and_25_out, not_2_out, not_4_out);
  and and_26 (and_26_out, c, not_4_out);
  and and_27 (and_27_out, a, c);
  and and_28 (and_28_out, a, b);
  and and_29 (and_29_out, not_3_out, not_4_out);
  and and_30 (and_30_out, not_1_out, b, not_3_out);
  and and_31 (and_31_out, b, not_4_out);
  and and_32 (and_32_out, a, not_2_out);
  and and_33 (and_33_out, a, c);
  and and_34 (and_34_out, not_2_out, c);
  and and_35 (and_35_out, a, not_2_out);
  and and_36 (and_36_out, not_1_out, b, not_3_out);
  and and_37 (and_37_out, not_1_out, b, not_4_out);
  and and_38 (and_38_out, b, not_3_out, d);
  and and_39 (and_39_out, c, not_4_out);
  and and_40 (and_40_out, a, d);
  or or_1 (seg1, and_1_out, and_2_out, and_3_out, and_4_out, and_5_out, and_6_out);
  or or_2 (seg2, and_7_out, and_8_out, and_9_out, and_10_out, and_11_out);
  or or_3 (seg3, and_12_out, and_13_out, and_14_out, and_15_out, and_16_out);
  or or_4 (seg4, and_17_out, and_18_out, and_19_out, and_20_out, and_21_out, and_22_out, and_23_out, and_24_out);
  or or_5 (seg5, and_25_out, and_26_out, and_27_out, and_28_out);
  or or_6 (seg6, and_29_out, and_30_out, and_31_out, and_32_out, and_33_out);
  or or_7 (seg7, and_34_out, and_35_out, and_36_out, and_37_out, and_38_out, and_39_out, and_40_out);
endmodule
