// Logisim project Labotest_2022.circ as structural Verilog: 7 circuits, main circuit VGA_ctrl
module VGA_ctrl (
  input  [11:0] pixel_in,
  input  clk,
  input  reset,
  output [11:0] pixel,
  output hsync,
  output vsync,
  output [9:0] H_out,
  output [8:0] V_out,
  output frame
);

  wire blank, comparator_1_gt, comparator_2_gt, comparator_3_gt, comparator_4_gt, h_counter_carry, not_1_out,
       not_2_out, v_counter_carry;
  wire [1:0] subtractor_1_out;
  wire [9:0] v_counter_q;
  wire [9:9] subtractor_2_out;
  wire [11:0] h_counter_q, multiplexer_1_out;

  Counter #(.max('hc6a), .width(12)) h_counter (
    .clr(reset), .load(1'b0), .up(1'b1), .count(1'b1), .clk(clk), .D({12{1'b0}}), .carry(h_counter_carry),
    .Q(h_counter_q));
  Counter #(.max('h20d), .width(10)) v_counter (
    .clr(reset), .load(1'b0), .up(1'b1), .count(h_counter_carry), .clk(clk), .carry(v_counter_carry),
    .Q(v_counter_q));  // open: D
  Comparator #(.mode("unsigned"), .width(12)) comparator_1 (
    .a(h_counter_q), .b(12'haee), .gt(comparator_1_gt));  // open: eq, lt
  not not_1 (not_1_out, comparator_1_gt);
  D_Flip_Flop d_ff_1 (.D(not_1_out), .clk(clk), .Q(hsync));  // open: Qn, preset, reset
  // Probe on v_counter_q
  Comparator #(.mode("unsigned"), .width(10)) comparator_2 (
    .a(v_counter_q), .b(10'h20b), .gt(comparator_2_gt));  // open: eq, lt
  D_Flip_Flop d_ff_2 (.D(not_2_out), .clk(clk), .Q(vsync));  // open: Qn, preset, reset
  not not_2 (not_2_out, comparator_2_gt);
  Subtractor #(.width(12)) subtractor_1 (
    .a(h_counter_q), .b(12'h40), .out({H_out, subtractor_1_out}));  // open: bin, bout
  Subtractor #(.width(10)) subtractor_2 (
    .a(v_counter_q), .b(10'h11), .out({subtractor_2_out[9], V_out}));  // open: bin, bout
  and and_1 (frame, v_counter_carry, h_counter_carry);
  Multiplexer #(.enable("false"), .width(12)) multiplexer_1 (
    .in0(pixel_in), .in1({12{1'b0}}), .out(multiplexer_1_out), .sel(blank));
  Comparator #(.mode("unsigned"), .width(12)) comparator_3 (
    .a({H_out, subtractor_1_out}), .b(12'h9ff), .gt(comparator_3_gt));  // open: eq, lt
  Comparator #(.mode("unsigned"), .width(10)) comparator_4 (
    .a({subtractor_2_out[9], V_out}), .b(10'h1df), .gt(comparator_4_gt));  // open: eq, lt
  Register #(.width(12)) register_1 (.D(multiplexer_1_out), .en(1'b1), .clk(clk), .Q(pixel), .clr(reset));
  or or_1 (blank, comparator_3_gt, comparator_4_gt);

  // Other names for the same wires on the sheet: pixel_int[11:0] = pixel_in

  // Notes on the sheet:
  //   vsync: pull=up
  //   pixel: pull=up
  //   hsync: pull=up
  //   Ne pas modifier ce circuit!!!!!
  //   Contrôle VGA 640 x 480 @ 60 Hz
endmodule

module Exercise (
  input  [9:0] H_in,
  input  [8:0] V_in,
  input  [7:0] SW,
  output [11:0] Pixel,
  output [6:0] Affichage_7_Seg
);


  assign Affichage_7_Seg = SW[6:0];
  assign Pixel = {12{1'b1}};

  // Notes on the sheet:
  //   Coordonnée horizontale, valeurs entre 0 et 639
  //   Coordonnée verticale, valeurs entre 0 et 479
endmodule

module Image_Gen (
  input  clk,
  input  reset,
  input  [7:0] SW,
  output [11:0] pixel,
  output hsync,
  output vsync,
  output [6:0] Affichage_7_Seg
);

  wire [8:0] VGA_v_out;
  wire [9:0] VGA_h_out;
  wire [11:0] Drapeaux_pixel;

  VGA_ctrl VGA (
    .pixel_in(Drapeaux_pixel), .clk(clk), .reset(reset), .pixel(pixel), .hsync(hsync), .vsync(vsync),
    .H_out(VGA_h_out), .V_out(VGA_v_out));  // open: frame
  Exercise Drapeaux (
    .H_in(VGA_h_out), .V_in(VGA_v_out), .SW(SW), .Pixel(Drapeaux_pixel), .Affichage_7_Seg(Affichage_7_Seg));

  // Notes on the sheet:
  //   vsync: pull=up
  //   hsync: pull=up
  //   pixel: pull=up
  //   Ne pas modifier ce circuit!!!!!
endmodule

module SIM_VGA_ctrl (
  input  rst,
  input  clk,
  output [4:0] H_out,
  output [4:0] V_out,
  output frame,
  output blank
);

  wire h_counter_carry, v_counter_carry;

  Counter #(.max('h1f), .width(5)) h_counter (
    .clr(rst), .load(1'b0), .up(1'b1), .count(1'b1), .clk(clk), .carry(h_counter_carry), .Q(H_out));  // open: D
  Counter #(.max('h1f), .width(5)) v_counter (
    .clr(rst), .load(1'b0), .up(1'b1), .count(h_counter_carry), .clk(clk), .carry(v_counter_carry), .Q(V_out));  // open: D
  Comparator #(.mode("unsigned"), .width(5)) comparator_1 (.a(V_out), .b(5'b10111), .gt(blank));  // open: eq, lt
  and and_1 (frame, v_counter_carry, h_counter_carry);

  // Notes on the sheet:
  //   Ne pas modifier ce circuit!!!!!
endmodule

module SIM_image_Gen (
  input  rst,
  input  clk,
  input  [7:0] Switch,
  output [4:0] H_count,
  output [4:0] V_count,
  output [2:0] Pixel,
  output [6:0] Affichage_7_Seg
);

  wire sim_vga_ctrl_1_blank;
  wire [3:0] undriven;
  wire [4:0] sim_scaler_1_out_2, sim_scaler_2_out_2;
  wire [9:0] undriven_2;
  wire [11:0] exercise_1_pixel;

  SIM_VGA_ctrl sim_vga_ctrl_1 (
    .rst(rst), .clk(clk), .H_out(H_count), .V_out(V_count), .blank(sim_vga_ctrl_1_blank));  // open: frame
  SIM_scaler sim_scaler_1 (.in_1(H_count), .out_2(sim_scaler_1_out_2));
  SIM_scaler sim_scaler_2 (.in_1(V_count), .out_2(sim_scaler_2_out_2));
  Exercise exercise_1 (
    .H_in({undriven_2[9], sim_scaler_1_out_2, undriven_2[3:0]}), .V_in({sim_scaler_2_out_2, undriven}),
    .SW(Switch), .Pixel(exercise_1_pixel), .Affichage_7_Seg(Affichage_7_Seg));
  Multiplexer #(.enable("false"), .width(3)) multiplexer_1 (
    .in0({exercise_1_pixel[11], exercise_1_pixel[7], exercise_1_pixel[3]}), .in1(3'b000), .out(Pixel),
    .sel(sim_vga_ctrl_1_blank));

  // Notes on the sheet:
  //   Ne pas modifier ce circuit!!!!!
endmodule

module SIM_console (
  input  reset,
  input  [7:0] Switch
);

  wire clk_out;
  wire [2:0] rgb_video_1_p6;
  wire [4:0] rgb_video_1_p4, rgb_video_1_p5;
  wire [6:0] sim_image_gen_1_affichage_7_seg;

  Clock clk (.out(clk_out));
  // RGB_Video #(.height(32), .reset("Synchronous"), .scale(8), .width(32)) rgb_video_1: pin names not known; wires that end beside it: reset, clk_out, 1'b1, rgb_video_1_p4, rgb_video_1_p5, rgb_video_1_p6
  SIM_image_Gen sim_image_gen_1 (
    .rst(reset), .clk(clk_out), .Switch(Switch), .H_count(rgb_video_1_p4), .V_count(rgb_video_1_p5),
    .Pixel(rgb_video_1_p6), .Affichage_7_Seg(sim_image_gen_1_affichage_7_seg));
  _7_Segment_Display u_7_segment_display_1 (
    .g(sim_image_gen_1_affichage_7_seg[0]), .f(sim_image_gen_1_affichage_7_seg[1]),
    .a(sim_image_gen_1_affichage_7_seg[6]), .b(sim_image_gen_1_affichage_7_seg[5]),
    .e(sim_image_gen_1_affichage_7_seg[2]), .d(sim_image_gen_1_affichage_7_seg[3]),
    .c(sim_image_gen_1_affichage_7_seg[4]));  // open: dp

  // Notes on the sheet:
  //   Ne pas modifier ce circuit!!!!!
endmodule

module SIM_scaler (
  input  [4:0] in_1,
  output [4:0] out_2
);

  wire [6:0] bit_extender_1_out, multiplier_1_out;
  wire [6:5] divider_1_out;

  assign bit_extender_1_out = {{2{1'b0}}, in_1};  // Bit_Extender bit_extender_1
  Multiplier #(.width(7)) multiplier_1 (
    .a(bit_extender_1_out), .b(7'b0000100), .out(multiplier_1_out));  // open: cin, cout
  Divider #(.width(7)) divider_1 (
    .a(multiplier_1_out), .b(7'b0000011), .out({divider_1_out, out_2}));  // open: upper, rem
endmodule
