// Logisim project SIM_Console_128_96.circ as structural Verilog
module VGA_ctrl (
  input  [11:0] pixel_in,
  input  clk,
  input  reset,
  output [11:0] pixel,
  output hsync,
  output vsync,
  output [9:0] H_out,
  output [8:0] V_out,
  output frame
);

  wire blank, comparator_1_gt, comparator_2_gt, comparator_3_gt, comparator_4_gt, h_counter_carry, not_1_out,
       not_2_out, v_counter_carry;
  wire [1:0] subtractor_1_out;
  wire [9:0] v_counter_q;
  wire [9:9] subtractor_2_out;
  wire [11:0] h_counter_q, multiplexer_1_out;

  Counter #(.max('hc6a), .width(12)) h_counter (
    .clr(reset), .load(1'b0), .up(1'b1), .count(1'b1), .clk(clk), .D({12{1'b0}}), .carry(h_counter_carry),
    .Q(h_counter_q));
  Counter #(.max('h20d), .width(10)) v_counter (
    .clr(reset), .load(1'b0), .up(1'b1), .count(h_counter_carry), .clk(clk), .carry(v_counter_carry),
    .Q(v_counter_q));  // open: D
  Comparator #(.mode("unsigned"), .width(12)) comparator_1 (
    .a(h_counter_q), .b(12'haee), .gt(comparator_1_gt));  // open: eq, lt
  not not_1 (not_1_out, comparator_1_gt);
  D_Flip_Flop d_ff_1 (.D(not_1_out), .clk(clk), .Q(hsync));  // open: Qn, preset, reset
  // Probe on v_counter_q
  Comparator #(.mode("unsigned"), .width(10)) comparator_2 (
    .a(v_counter_q), .b(10'h20b), .gt(comparator_2_gt));  // open: eq, lt
  D_Flip_Flop d_ff_2 (.D(not_2_out), .clk(clk), .Q(vsync));  // open: Qn, preset, reset
  not not_2 (not_2_out, comparator_2_gt);
  Subtractor #(.width(12)) subtractor_1 (
    .a(h_counter_q), .b(12'h40), .out({H_out, subtractor_1_out}));  // open: bin, bout
  Subtractor #(.width(10)) subtractor_2 (
    .a(v_counter_q), .b(10'h11), .out({subtractor_2_out[9], V_out}));  // open: bin, bout
  and and_1 (frame, v_counter_carry, h_counter_carry);
  Multiplexer #(.width(12)) multiplexer_1 (.in0(pixel_in), .in1({12{1'b0}}), .out(multiplexer_1_out), .sel(blank));
  Comparator #(.mode("unsigned"), .width(12)) comparator_3 (
    .a({H_out, subtractor_1_out}), .b(12'h9ff), .gt(comparator_3_gt));  // open: eq, lt
  Comparator #(.mode("unsigned"), .width(10)) comparator_4 (
    .a({subtractor_2_out[9], V_out}), .b(10'h1df), .gt(comparator_4_gt));  // open: eq, lt
  Register #(.width(12)) register_1 (.D(multiplexer_1_out), .en(1'b1), .clk(clk), .Q(pixel), .clr(reset));
  or or_1 (blank, comparator_3_gt, comparator_4_gt);

  // Other names for the same wires on the sheet: pixel_int[11:0] = pixel_in

  // Notes on the sheet:
  //   vsync: pull=up
  //   pixel: pull=up
  //   hsync: pull=up
  //   Ne pas modifier ce circuit!!!!!
  //   Ne pas modifier ce circuit!!!!!
  //   Contrôle VGA 640 x 480 @ 60 Hz
  //   Ne pas modifier ce circuit!!!!!
endmodule

module Image_Gen (
  input  clk,
  input  reset,
  input  [7:0] SW,
  output [11:0] pixel,
  output hsync,
  output vsync
);

  wire [8:0] VGA_v_out;
  wire [9:0] VGA_h_out;
  wire [11:0] undriven;

  VGA_ctrl VGA (
    .pixel_in(undriven), .clk(clk), .reset(reset), .pixel(pixel), .hsync(hsync), .vsync(vsync),
    .H_out(VGA_h_out), .V_out(VGA_v_out));  // open: frame
  Exercise Drapeaux ();

  // Notes on the sheet:
  //   vsync: pull=up
  //   hsync: pull=up
  //   pixel: pull=up
  //   Ne pas modifier ce circuit!!!!!
  //   Ne pas modifier ce circuit!!!!!
endmodule

module SIM_VGA_ctrl (
  input  rst,
  input  clk,
  output [6:0] H_out,
  output [6:0] V_out,
  output frame,
  output blank
);

  wire h_counter_carry, v_counter_carry;

  Counter #(.max('h7f), .width(7)) h_counter (
    .clr(rst), .load(1'b0), .up(1'b1), .count(1'b1), .clk(clk), .carry(h_counter_carry), .Q(H_out));  // open: D
  Counter #(.max('h5f), .width(7)) v_counter (
    .clr(rst), .load(1'b0), .up(1'b1), .count(h_counter_carry), .clk(clk), .carry(v_counter_carry), .Q(V_out));  // open: D
  // Probe on H_out
  Comparator #(.mode("unsigned"), .width(7)) comparator_1 (.a(V_out), .b(7'b1011111), .gt(blank));  // open: eq, lt
  and and_1 (frame, v_counter_carry, h_counter_carry);

  // Notes on the sheet:
  //   Ne pas modifier ce circuit!!!!!
endmodule

module SIM_image_Gen (
  input  rst,
  input  clk,
  input  [1:0] Switch,
  output [6:0] H_count,
  output [6:0] V_count,
  output [2:0] Pixel
);

  wire sim_vga_ctrl_1_blank;
  wire [2:0] undriven;

  SIM_VGA_ctrl sim_vga_ctrl_1 (
    .rst(rst), .clk(clk), .H_out(H_count), .V_out(V_count), .blank(sim_vga_ctrl_1_blank));  // open: frame
  // Probe on V_count
  Exercise exercise_1 ();
  Multiplexer #(.width(3)) multiplexer_1 (.in0(undriven), .in1(3'b000), .out(Pixel), .sel(sim_vga_ctrl_1_blank));

  // Notes on the sheet:
  //   Ne pas modifier ce circuit!!!!!
  //   Ne pas modifier ce circuit!!!!!
endmodule

module SIM_console (
  input  reset,
  input  [1:0] Switch,
  input  [3:0] in_3
);

  wire clk_out, dec_7_1_seg1, dec_7_1_seg2, dec_7_1_seg3, dec_7_1_seg4, dec_7_1_seg5, dec_7_1_seg6,
       dec_7_1_seg7;
  wire [2:0] rgb_video_1_p6;
  wire [6:0] rgb_video_1_p4, rgb_video_1_p5;
  wire [8:0] seven_to_nine_1_nine, seven_to_nine_2_nine;
  wire [10:0] buttons_1_d_c;

  Clock clk (.out(clk_out));
  // RGB_Video #(.height(96), .reset("Synchronous"), .scale(5), .width(127)) rgb_video_1: pin names not known; wires that end beside it: reset, clk_out, 1'b1, rgb_video_1_p4, rgb_video_1_p5, rgb_video_1_p6
  SIM_image_Gen sim_image_gen_1 (
    .rst(reset), .clk(clk_out), .Switch(Switch), .H_count(rgb_video_1_p4), .V_count(rgb_video_1_p5));  // open: Pixel
  // Probe on rgb_video_1_p5
  // Probe on rgb_video_1_p4
  Seven_to_Nine seven_to_nine_1 (.Seven(rgb_video_1_p4), .Nine(seven_to_nine_1_nine));
  Seven_to_Nine seven_to_nine_2 (.Seven(rgb_video_1_p5), .Nine(seven_to_nine_2_nine));
  // Probe on seven_to_nine_2_nine
  // Probe on seven_to_nine_1_nine
  Buttons buttons_1 (
    .H_in(seven_to_nine_1_nine), .SW(in_3), .V_in(seven_to_nine_2_nine),
    .D_C({rgb_video_1_p6[2], buttons_1_d_c[10:8], rgb_video_1_p6[1], buttons_1_d_c[6:4], rgb_video_1_p6[0], buttons_1_d_c[2:0]}));
  Dec_7 dec_7_1 (
    .a(in_3[3]), .b(in_3[2]), .c(in_3[1]), .d(in_3[0]), .seg1(dec_7_1_seg1), .seg2(dec_7_1_seg2),
    .seg3(dec_7_1_seg3), .seg4(dec_7_1_seg4), .seg5(dec_7_1_seg5), .seg6(dec_7_1_seg6), .seg7(dec_7_1_seg7));
  _7_Segment_Display u_7_segment_display_1 (
    .g(dec_7_1_seg7), .f(dec_7_1_seg6), .a(dec_7_1_seg1), .b(dec_7_1_seg2), .e(dec_7_1_seg5),
    .d(dec_7_1_seg4), .c(dec_7_1_seg3));  // open: dp

  // Notes on the sheet:
  //   Ne pas modifier ce circuit!!!!!
  //   Ne pas modifier ce circuit!!!!!
endmodule

module SIM_hscaler (
  input  [6:0] in_1,
  output [6:0] out_2
);

  wire [8:0] bit_extender_1_out, multiplier_1_out;
  wire [8:7] divider_1_out;

  assign bit_extender_1_out = {{2{1'b0}}, in_1};  // Bit_Extender bit_extender_1
  Multiplier #(.width(9)) multiplier_1 (.a(bit_extender_1_out), .b(9'h4), .out(multiplier_1_out));  // open: cin, cout
  Divider #(.width(9)) divider_1 (.a(multiplier_1_out), .b(9'h3), .out({divider_1_out, out_2}));  // open: upper, rem

  // Notes on the sheet:
  //   Ne pas modifier ce circuit!!!!!
endmodule

module SIM_vscaler (
  input  [6:0] in_1,
  output [6:0] out_2
);

  wire [8:0] bit_extender_1_out, multiplier_1_out;
  wire [8:7] divider_1_out;

  assign bit_extender_1_out = {{2{1'b0}}, in_1};  // Bit_Extender bit_extender_1
  Multiplier #(.width(9)) multiplier_1 (.a(bit_extender_1_out), .b(9'h4), .out(multiplier_1_out));  // open: cin, cout
  Divider #(.width(9)) divider_1 (.a(multiplier_1_out), .b(9'h3), .out({divider_1_out, out_2}));  // open: upper, rem

  // Notes on the sheet:
  //   Ne pas modifier ce circuit!!!!!
endmodule

module Red_White (
  input  Rouge,
  input  Blanc,
  output R,
  output B
);

  wire not_1_out;

  not not_1 (not_1_out, Blanc);
  and and_1 (R, Rouge, not_1_out);

  assign B = Blanc;
endmodule

module Vaud (
  input  [6:0] V,
  output [11:0] pixel
);

  wire comparator_1_gt;

  Comparator #(.mode("unsigned"), .width(7)) comparator_1 (
    .a(V), .b(7'b0110000), .gt(comparator_1_gt));  // open: eq, lt
  Multiplexer #(.width(12)) multiplexer_1 (.in0({12{1'b1}}), .in1(12'hf0), .out(pixel), .sel(comparator_1_gt));
endmodule

module Tcheque (
  input  [8:0] V_in,
  input  [8:0] H_in,
  output [11:0] D_T
);

  wire and_1_out, comparator_1_gt, comparator_2_gt, comparator_3_gt;
  wire [8:0] subtractor_1_out;
  wire [11:0] multiplexer_1_out;

  Subtractor #(.width(9)) subtractor_1 (.a(9'h60), .b(V_in), .out(subtractor_1_out));  // open: bin, bout
  Comparator #(.mode("unsigned"), .width(9)) comparator_1 (.a(V_in), .b(H_in), .gt(comparator_1_gt));  // open: eq, lt
  Comparator #(.mode("unsigned"), .width(9)) comparator_2 (
    .a(subtractor_1_out), .b(H_in), .gt(comparator_2_gt));  // open: eq, lt
  and and_1 (and_1_out, comparator_1_gt, comparator_2_gt);
  Comparator #(.mode("unsigned"), .width(9)) comparator_3 (.a(V_in), .b(9'h30), .gt(comparator_3_gt));  // open: eq, lt
  Multiplexer #(.width(12)) multiplexer_1 (
    .in0({12{1'b1}}), .in1(12'hf00), .out(multiplexer_1_out), .sel(comparator_3_gt));
  Multiplexer #(.width(12)) multiplexer_2 (.in0(multiplexer_1_out), .in1(12'hf), .out(D_T), .sel(and_1_out));
endmodule

module Suisse (
  input  [6:0] H_in,
  input  [6:0] V_in,
  output [11:0] D_S
);

  wire and_1_out, and_2_out, and_3_out, and_4_out, and_5_out, and_6_out, comparator_1_gt, comparator_2_lt,
       comparator_3_gt, comparator_4_lt, comparator_5_gt, comparator_6_lt, comparator_7_gt, comparator_8_lt,
       comparator_9_gt, or_1_out;
  wire [11:0] multiplexer_1_out;

  Comparator #(.mode("unsigned"), .width(7)) comparator_1 (
    .a(V_in), .b(7'b0100111), .gt(comparator_1_gt));  // open: eq, lt
  Comparator #(.mode("unsigned"), .width(7)) comparator_2 (
    .a(V_in), .b(7'b0111001), .lt(comparator_2_lt));  // open: gt, eq
  Comparator #(.mode("unsigned"), .width(7)) comparator_3 (
    .a(H_in), .b(7'b0010001), .gt(comparator_3_gt));  // open: eq, lt
  Comparator #(.mode("unsigned"), .width(7)) comparator_4 (
    .a(H_in), .b(7'b1001111), .lt(comparator_4_lt));  // open: gt, eq
  Comparator #(.mode("unsigned"), .width(7)) comparator_5 (
    .a(V_in), .b(7'b0010001), .gt(comparator_5_gt));  // open: eq, lt
  Comparator #(.mode("unsigned"), .width(7)) comparator_6 (
    .a(V_in), .b(7'b1001111), .lt(comparator_6_lt));  // open: gt, eq
  Comparator #(.mode("unsigned"), .width(7)) comparator_7 (
    .a(H_in), .b(7'b0100111), .gt(comparator_7_gt));  // open: eq, lt
  Comparator #(.mode("unsigned"), .width(7)) comparator_8 (
    .a(H_in), .b(7'b0111001), .lt(comparator_8_lt));  // open: gt, eq
  and and_1 (and_1_out, comparator_1_gt, comparator_2_lt);
  and and_2 (and_2_out, comparator_3_gt, comparator_4_lt);
  and and_3 (and_3_out, comparator_5_gt, comparator_6_lt);
  and and_4 (and_4_out, comparator_7_gt, comparator_8_lt);
  and and_5 (and_5_out, and_1_out, and_2_out);
  and and_6 (and_6_out, and_3_out, and_4_out);
  Comparator #(.mode("unsigned"), .width(7)) comparator_9 (
    .a(H_in), .b(7'b1100000), .gt(comparator_9_gt));  // open: eq, lt
  Multiplexer #(.width(12)) multiplexer_1 (.in0(12'hf00), .in1({12{1'b1}}), .out(multiplexer_1_out), .sel(or_1_out));
  or or_1 (or_1_out, and_5_out, and_6_out);
  Multiplexer #(.width(12)) multiplexer_2 (.in0(multiplexer_1_out), .in1({12{1'b0}}), .out(D_S), .sel(comparator_9_gt));
endmodule

module Suede (
  input  [8:0] H_in,
  input  [8:0] V_in,
  output [11:0] D_S
);

  wire and_1_out, and_2_out, comparator_1_gt, comparator_2_lt, comparator_3_gt, comparator_4_lt, or_1_out;

  Comparator #(.mode("unsigned"), .width(9)) comparator_1 (.a(H_in), .b(9'h28), .gt(comparator_1_gt));  // open: eq, lt
  Comparator #(.mode("unsigned"), .width(9)) comparator_2 (.a(H_in), .b(9'h38), .lt(comparator_2_lt));  // open: gt, eq
  Comparator #(.mode("unsigned"), .width(9)) comparator_3 (.a(V_in), .b(9'h27), .gt(comparator_3_gt));  // open: eq, lt
  Comparator #(.mode("unsigned"), .width(9)) comparator_4 (.a(V_in), .b(9'h39), .lt(comparator_4_lt));  // open: gt, eq
  and and_1 (and_1_out, comparator_1_gt, comparator_2_lt);
  and and_2 (and_2_out, comparator_3_gt, comparator_4_lt);
  or or_1 (or_1_out, and_1_out, and_2_out);
  Multiplexer #(.width(12)) multiplexer_1 (.in0(12'hf), .in1(12'hff0), .out(D_S), .sel(or_1_out));
endmodule

module France (
  input  [6:0] H_in,
  output [11:0] D_F
);

  wire comparator_1_gt, comparator_2_lt;
  wire [11:0] multiplexer_1_out;

  Comparator #(.mode("unsigned"), .width(7)) comparator_1 (
    .a(H_in), .b(7'b1010101), .gt(comparator_1_gt));  // open: eq, lt
  Comparator #(.mode("unsigned"), .width(7)) comparator_2 (
    .a(H_in), .b(7'b0101011), .lt(comparator_2_lt));  // open: gt, eq
  Multiplexer #(.width(12)) multiplexer_1 (
    .in0({12{1'b1}}), .in1(12'hf), .out(multiplexer_1_out), .sel(comparator_2_lt));
  Multiplexer #(.width(12)) multiplexer_2 (.in0(multiplexer_1_out), .in1(12'hf00), .out(D_F), .sel(comparator_1_gt));
endmodule

module Congo (
  input  [8:0] H_in,
  input  [8:0] V_in,
  output [11:0] D_C
);

  wire comparator_1_lt, comparator_2_lt;
  wire [8:0] subtractor_1_out, subtractor_2_out;
  wire [11:0] multiplexer_1_out;

  Subtractor #(.width(9)) subtractor_1 (.a(9'h60), .b(V_in), .out(subtractor_1_out));  // open: bin, bout
  Subtractor #(.width(9)) subtractor_2 (.a(9'h80), .b(V_in), .out(subtractor_2_out));  // open: bin, bout
  Comparator #(.mode("unsigned"), .width(9)) comparator_1 (
    .a(H_in), .b(subtractor_1_out), .lt(comparator_1_lt));  // open: gt, eq
  Comparator #(.mode("unsigned"), .width(9)) comparator_2 (
    .a(H_in), .b(subtractor_2_out), .lt(comparator_2_lt));  // open: gt, eq
  Multiplexer #(.width(12)) multiplexer_1 (.in0(12'hff0), .in1(12'hf0), .out(multiplexer_1_out), .sel(comparator_1_lt));
  Multiplexer #(.width(12)) multiplexer_2 (.in0(12'hf00), .in1(multiplexer_1_out), .out(D_C), .sel(comparator_2_lt));
endmodule

module Seven_to_Nine (
  input  [6:0] Seven,
  output [8:0] Nine
);


  assign Nine = {2'b00, Seven};
endmodule

module CongoRad (
  input  [8:0] H_in,
  input  [8:0] V_in,
  output [11:0] D_C
);

  wire comparator_1_lt, comparator_2_gt;
  wire [8:0] subtractor_1_out, subtractor_2_out;
  wire [11:0] multiplexer_1_out;

  Subtractor #(.width(9)) subtractor_1 (.a(9'h60), .b(V_in), .out(subtractor_1_out));  // open: bin, bout
  Comparator #(.width(9)) comparator_1 (.a(H_in), .b(subtractor_1_out), .lt(comparator_1_lt));  // open: gt, eq
  Subtractor #(.width(9)) subtractor_2 (.a(H_in), .b(9'h24), .out(subtractor_2_out));  // open: bin, bout
  Multiplexer #(.width(12)) multiplexer_1 (.in0(12'hf0), .in1(12'hff0), .out(multiplexer_1_out), .sel(comparator_1_lt));
  Comparator #(.width(9)) comparator_2 (
    .a(subtractor_2_out), .b(subtractor_1_out), .gt(comparator_2_gt));  // open: eq, lt
  Multiplexer #(.width(12)) multiplexer_2 (.in0(multiplexer_1_out), .in1(12'hf00), .out(D_C), .sel(comparator_2_gt));
endmodule

module Buttons (
  input  [8:0] H_in,
  input  [3:0] SW,
  input  [8:0] V_in,
  output [11:0] D_C
);

  wire [11:0] carre_1_pixel, carre_2_pixel, carre_3_pixel, carre_4_pixel;

  Carre carre_1 (
    .H_in(H_in), .Start_h(9'hc), .SW(SW[3]), .Stop_h(9'h1c), .V_in(V_in), .Start_v(9'h20), .Stop_v(9'h40),
    .pixel(carre_1_pixel));
  Carre carre_2 (
    .H_in(H_in), .Start_h(9'h28), .SW(SW[2]), .Stop_h(9'h38), .V_in(V_in), .Start_v(9'h20), .Stop_v(9'h40),
    .pixel(carre_2_pixel));
  Carre carre_3 (
    .H_in(H_in), .Start_h(9'h45), .SW(SW[1]), .Stop_h(9'h54), .V_in(V_in), .Start_v(9'h20), .Stop_v(9'h40),
    .pixel(carre_3_pixel));
  Carre carre_4 (
    .H_in(H_in), .Start_h(9'h60), .SW(SW[0]), .Stop_h(9'h70), .V_in(V_in), .Start_v(9'h20), .Stop_v(9'h40),
    .pixel(carre_4_pixel));
  assign D_C = carre_1_pixel | carre_2_pixel | carre_3_pixel | carre_4_pixel;  // OR_Gate or_1, 12 bits wide
endmodule

module Carre (
  input  [8:0] H_in,
  input  [8:0] Start_h,
  input  SW,
  input  [8:0] Stop_h,
  input  [8:0] V_in,
  input  [8:0] Start_v,
  input  [8:0] Stop_v,
  output [11:0] pixel
);

  wire and_1_out, and_2_out, and_3_out, comparator_1_gt, comparator_2_lt, comparator_3_gt, comparator_4_lt;
  wire [11:0] multiplexer_1_out;

  Comparator #(.mode("unsigned"), .width(9)) comparator_1 (
    .a(H_in), .b(Start_h), .gt(comparator_1_gt));  // open: eq, lt
  Comparator #(.mode("unsigned"), .width(9)) comparator_2 (.a(H_in), .b(Stop_h), .lt(comparator_2_lt));  // open: gt, eq
  Comparator #(.mode("unsigned"), .width(9)) comparator_3 (
    .a(V_in), .b(Start_v), .gt(comparator_3_gt));  // open: eq, lt
  Comparator #(.mode("unsigned"), .width(9)) comparator_4 (.a(V_in), .b(Stop_v), .lt(comparator_4_lt));  // open: gt, eq
  and and_1 (and_1_out, comparator_1_gt, comparator_2_lt);
  and and_2 (and_2_out, comparator_3_gt, comparator_4_lt);
  Multiplexer #(.width(12)) multiplexer_1 (.in0(12'hff0), .in1(12'hf), .out(multiplexer_1_out), .sel(SW));
  and and_3 (and_3_out, and_1_out, and_2_out);
  Multiplexer #(.width(12)) multiplexer_2 (.in0(12'h666), .in1(multiplexer_1_out), .out(pixel), .sel(and_3_out));
endmodule

module Dec_7 (
  input  a,
  input  b,
  input  c,
  input  d,
  output seg1,
  output seg2,
  output seg3,
  output seg4,
  output seg5,
  output seg6,
  output seg7
);

  wire and_1_out, and_2_out, and_3_out, and_4_out, and_5_out, and_6_out, and_7_out, and_8_out, and_9_out,
       and_10_out, and_11_out, and_12_out, and_13_out, and_14_out, and_15_out, and_16_out, and_17_out,
       and_18_out, and_19_out, and_20_out, and_21_out, and_22_out, and_23_out, and_24_out, and_25_out,
       and_26_out, and_27_out, and_28_out, and_29_out, and_30_out, and_31_out, and_32_out, and_33_out,
       and_34_out, and_35_out, and_36_out, and_37_out, and_38_out, and_39_out, and_40_out, not_1_out,
       not_2_out, not_3_out, not_4_out;

  not not_1 (not_1_out, a);
  not not_2 (not_2_out, b);
  not not_3 (not_3_out, c);
  not not_4 (not_4_out, d);
  and and_1 (and_1_out, not_2_out, not_4_out);
  and and_2 (and_2_out, not_1_out, c);
  and and_3 (and_3_out, not_1_out, b, d);
  and and_4 (and_4_out, a, not_2_out, not_3_out);
  and and_5 (and_5_out, a, not_4_out);
  and and_6 (and_6_out, b, c);
  and and_7 (and_7_out, not_1_out, not_3_out, not_4_out);
  and and_8 (and_8_out, not_1_out, c, d);
  and and_9 (and_9_out, not_2_out, not_4_out);
  and and_10 (and_10_out, a, not_3_out, d);
  and and_11 (and_11_out, not_1_out, not_2_out);
  and and_12 (and_12_out, not_1_out, b);
  and and_13 (and_13_out, a, not_2_out);
  and and_14 (and_14_out, not_3_out, d);
  and and_15 (and_15_out, not_1_out, not_3_out);
  and and_16 (and_16_out, not_1_out, d);
  and and_17 (and_17_out, b, not_3_out, d);
  and and_18 (and_18_out, not_1_out, not_2_out, not_4_out);
  and and_19 (and_19_out, not_1_out, not_2_out, c);
  and and_20 (and_20_out, not_1_out, c, not_4_out);
  and and_21 (and_21_out, not_2_out, not_3_out, not_4_out);
  and and_22 (and_22_out, a, not_3_out);
  and and_23 (and_23_out, not_2_out, c, d);
  and and_24 (and_24_out, b, c, not_4_out);
  and and_25 (and_25_out, not_2_out, not_4_out);
  and and_26 (and_26_out, c, not_4_out);
  and and_27 (and_27_out, a, c);
  and and_28 (and_28_out, a, b);
  and and_29 (and_29_out, not_3_out, not_4_out);
  and and_30 (and_30_out, not_1_out, b, not_3_out);
  and and_31 (and_31_out, b, not_4_out);
  and and_32 (and_32_out, a, not_2_out);
  and and_33 (and_33_out, a, c);
  and and_34 (and_34_out, not_2_out, c);
  and and_35 (and_35_out, a, not_2_out);
  and and_36 (and_36_out, not_1_out, b, not_3_out);
  and and_37 (and_37_out, not_1_out, b, not_4_out);
  and and_38 (and_38_out, b, not_3_out, d);
  and and_39 (and_39_out, c, not_4_out);
  and and_40 (and_40_out, a, d);
  or or_1 (seg1, and_1_out, and_2_out, and_3_out, and_4_out, and_5_out, and_6_out);
  or or_2 (seg2, and_7_out, and_8_out, and_9_out, and_10_out, and_11_out);
  or or_3 (seg3, and_12_out, and_13_out, and_14_out, and_15_out, and_16_out);
  or or_4 (seg4, and_17_out, and_18_out, and_19_out, and_20_out, and_21_out, and_22_out, and_23_out, and_24_out);
  or or_5 (seg5, and_25_out, and_26_out, and_27_out, and_28_out);
  or or_6 (seg6, and_29_out, and_30_out, and_31_out, and_32_out, and_33_out);
  or or_7 (seg7, and_34_out, and_35_out, and_36_out, and_37_out, and_38_out, and_39_out, and_40_out);
endmodule
