// Logisim project Sequentiels.circ as structural Verilog: 7 circuits, main circuit D_bascule
module D_bascule (
  input  D,
  input  clk,
  output Q
);

  wire d_ff_1_q;

  D_Flip_Flop d_ff_1 (.D(D), .clk(clk), .Q(d_ff_1_q));  // open: Qn, preset, reset
  D_Flip_Flop d_ff_2 (.D(d_ff_1_q), .clk(clk), .Q(Q));  // open: Qn, preset, reset
endmodule

module D_reg (
  input  WR,
  input  D,
  input  clk,
  output Q
);

  wire multiplexer_1_out;

  Multiplexer multiplexer_1 (.in0(Q), .in1(D), .out(multiplexer_1_out), .sel(WR));
  D_bascule d_bascule_1 (.D(multiplexer_1_out), .clk(clk), .Q(Q));
endmodule

module D_btn (
  input  D,
  input  clk,
  output Q
);

  wire and_1_out, d_ff_1_q;

  D_Flip_Flop d_ff_1 (.D(D), .clk(clk), .Q(d_ff_1_q));  // open: Qn, preset, reset
  and and_1 (and_1_out, ~D, d_ff_1_q);  // AND_Gate
  D_Flip_Flop d_ff_2 (.D(and_1_out), .clk(clk), .Q(Q));  // open: Qn, preset, reset
endmodule

module ControleLed (
  input  btn,
  input  clk
);

  wire d_btn_1_q, d_ff_1_q, multiplexer_1_out, not_1_out;

  D_btn d_btn_1 (.D(btn), .clk(clk), .Q(d_btn_1_q));
  Multiplexer multiplexer_1 (.in0(d_ff_1_q), .in1(not_1_out), .out(multiplexer_1_out), .sel(d_btn_1_q));
  not not_1 (not_1_out, d_ff_1_q);
  D_Flip_Flop d_ff_1 (.D(multiplexer_1_out), .clk(clk), .Q(d_ff_1_q));  // open: Qn, preset, reset
  LED led_1 (.in(d_ff_1_q));
endmodule

module Compteur (
  input  Enable,
  input  Reset_n,
  input  Up_Down_n,
  input  clk,
  output [7:0] Cnt
);

  wire not_1_out;
  wire [7:0] alusimple8bit_1_res, multiplexer_1_out, multiplexer_2_out;

  not not_1 (not_1_out, Up_Down_n);
  AluSimple8Bit alusimple8bit_1 (.OP(not_1_out), .A(Cnt), .B(8'h1), .Res(alusimple8bit_1_res));  // open: C_out, V_out
  Multiplexer #(.width(8)) multiplexer_1 (.in0(Cnt), .in1(alusimple8bit_1_res), .out(multiplexer_1_out), .sel(Enable));
  Multiplexer #(.width(8)) multiplexer_2 (
    .in0({8{1'b0}}), .in1(multiplexer_1_out), .out(multiplexer_2_out), .sel(Reset_n));
  Register register_1 (.D(multiplexer_2_out), .en(1'b1), .clk(clk), .Q(Cnt));  // open: clr

  // Other names for the same wires on the sheet: En = Enable; Rst = Reset_n; U_D = Up_Down_n
endmodule

module CompteurAutorisation (
  input  Incr,
  input  clk,
  input  Decr,
  input  Reset_n,
  output [7:0] Cnt
);

  wire up_down_decod_1_enable, up_down_decod_1_up_down_n;

  Up_Down_Decod up_down_decod_1 (
    .Incr(Incr), .clk(clk), .Decr(Decr), .Up_Down_n(up_down_decod_1_up_down_n),
    .Enable(up_down_decod_1_enable));
  Compteur compteur_1 (
    .Enable(up_down_decod_1_enable), .Reset_n(Reset_n), .Up_Down_n(up_down_decod_1_up_down_n), .clk(clk),
    .Cnt(Cnt));
endmodule

module Up_Down_Decod (
  input  Incr,
  input  clk,
  input  Decr,
  output Up_Down_n,
  output Enable
);

  wire d_btn_2_q;

  D_btn d_btn_1 (.D(Incr), .clk(clk), .Q(Up_Down_n));
  D_btn d_btn_2 (.D(Decr), .clk(clk), .Q(d_btn_2_q));
  xor xor_1 (Enable, Up_Down_n, d_btn_2_q);
endmodule
