// Logisim project TableMixage.circ as structural Verilog
module Simulateur (
);

  wire clock_1_out, clock_2_out, clock_3_out, clock_4_out, sample_clk_out;
  wire [1:0] undriven, undriven_2;
  wire [6:0] mixer_1_audio_out_2;
  wire [7:0] sinus_fast_out_2, sinus_slow_out_2;
  wire [7:7] mixer_1_audio_out, not_1_out, not_2_out, not_3_out;
  wire [31:0] decodeur_sim_1_out_3, decodeur_sim_1_out_4, decodeur_sim_1_out_5, decodeur_sim_1_out_6,
       decodeur_sim_1_out_7, decodeur_sim_1_out_8, decodeur_sim_1_out_9, decodeur_sim_1_out_10,
       decodeur_sim_1_out_11, decodeur_sim_1_out_12, decodeur_sim_1_out_13, decodeur_sim_1_out_14,
       decodeur_sim_1_out_15, decodeur_sim_1_out_16, decodeur_sim_1_out_17, decodeur_sim_1_out_18,
       decodeur_sim_1_out_19, decodeur_sim_1_out_20, decodeur_sim_1_out_21, decodeur_sim_1_out_22,
       decodeur_sim_1_out_23, decodeur_sim_1_out_24, decodeur_sim_1_out_25, decodeur_sim_1_out_26,
       decodeur_sim_1_out_27, decodeur_sim_1_out_28, decodeur_sim_1_out_29, decodeur_sim_1_out_30,
       decodeur_sim_1_out_31, decodeur_sim_1_out_32, decodeur_sim_1_out_33, decodeur_sim_1_out_34,
       decodeur_sim_1_out_35, decodeur_sim_1_out_36, decodeur_sim_1_out_37, decodeur_sim_1_out_38,
       decodeur_sim_1_out_39, decodeur_sim_1_out_40, decodeur_sim_1_out_41, decodeur_sim_1_out_42,
       decodeur_sim_1_out_43, decodeur_sim_1_out_44, decodeur_sim_1_out_45, decodeur_sim_1_out_46,
       decodeur_sim_1_out_47, decodeur_sim_1_out_48, decodeur_sim_1_out_49, decodeur_sim_1_out_50,
       decodeur_sim_1_out_51, decodeur_sim_1_out_52, decodeur_sim_1_out_53, decodeur_sim_1_out_54,
       decodeur_sim_1_out_55, decodeur_sim_1_out_56, decodeur_sim_1_out_57, decodeur_sim_1_out_58,
       decodeur_sim_1_out_59, decodeur_sim_1_out_60, decodeur_sim_1_out_61, decodeur_sim_1_out_62,
       decodeur_sim_1_out_63, decodeur_sim_1_out_64, decodeur_sim_1_out_65, decodeur_sim_1_out_66,
       decodeur_sim_2_out_3, decodeur_sim_2_out_4, decodeur_sim_2_out_5, decodeur_sim_2_out_6,
       decodeur_sim_2_out_7, decodeur_sim_2_out_8, decodeur_sim_2_out_9, decodeur_sim_2_out_10,
       decodeur_sim_2_out_11, decodeur_sim_2_out_12, decodeur_sim_2_out_13, decodeur_sim_2_out_14,
       decodeur_sim_2_out_15, decodeur_sim_2_out_16, decodeur_sim_2_out_17, decodeur_sim_2_out_18,
       decodeur_sim_2_out_19, decodeur_sim_2_out_20, decodeur_sim_2_out_21, decodeur_sim_2_out_22,
       decodeur_sim_2_out_23, decodeur_sim_2_out_24, decodeur_sim_2_out_25, decodeur_sim_2_out_26,
       decodeur_sim_2_out_27, decodeur_sim_2_out_28, decodeur_sim_2_out_29, decodeur_sim_2_out_30,
       decodeur_sim_2_out_31, decodeur_sim_2_out_32, decodeur_sim_2_out_33, decodeur_sim_2_out_34,
       decodeur_sim_2_out_35, decodeur_sim_2_out_36, decodeur_sim_2_out_37, decodeur_sim_2_out_38,
       decodeur_sim_2_out_39, decodeur_sim_2_out_40, decodeur_sim_2_out_41, decodeur_sim_2_out_42,
       decodeur_sim_2_out_43, decodeur_sim_2_out_44, decodeur_sim_2_out_45, decodeur_sim_2_out_46,
       decodeur_sim_2_out_47, decodeur_sim_2_out_48, decodeur_sim_2_out_49, decodeur_sim_2_out_50,
       decodeur_sim_2_out_51, decodeur_sim_2_out_52, decodeur_sim_2_out_53, decodeur_sim_2_out_54,
       decodeur_sim_2_out_55, decodeur_sim_2_out_56, decodeur_sim_2_out_57, decodeur_sim_2_out_58,
       decodeur_sim_2_out_59, decodeur_sim_2_out_60, decodeur_sim_2_out_61, decodeur_sim_2_out_62,
       decodeur_sim_2_out_63, decodeur_sim_2_out_64, decodeur_sim_2_out_65, decodeur_sim_2_out_66,
       decodeur_sim_3_out_3, decodeur_sim_3_out_4, decodeur_sim_3_out_5, decodeur_sim_3_out_6,
       decodeur_sim_3_out_7, decodeur_sim_3_out_8, decodeur_sim_3_out_9, decodeur_sim_3_out_10,
       decodeur_sim_3_out_11, decodeur_sim_3_out_12, decodeur_sim_3_out_13, decodeur_sim_3_out_14,
       decodeur_sim_3_out_15, decodeur_sim_3_out_16, decodeur_sim_3_out_17, decodeur_sim_3_out_18,
       decodeur_sim_3_out_19, decodeur_sim_3_out_20, decodeur_sim_3_out_21, decodeur_sim_3_out_22,
       decodeur_sim_3_out_23, decodeur_sim_3_out_24, decodeur_sim_3_out_25, decodeur_sim_3_out_26,
       decodeur_sim_3_out_27, decodeur_sim_3_out_28, decodeur_sim_3_out_29, decodeur_sim_3_out_30,
       decodeur_sim_3_out_31, decodeur_sim_3_out_32, decodeur_sim_3_out_33, decodeur_sim_3_out_34,
       decodeur_sim_3_out_35, decodeur_sim_3_out_36, decodeur_sim_3_out_37, decodeur_sim_3_out_38,
       decodeur_sim_3_out_39, decodeur_sim_3_out_40, decodeur_sim_3_out_41, decodeur_sim_3_out_42,
       decodeur_sim_3_out_43, decodeur_sim_3_out_44, decodeur_sim_3_out_45, decodeur_sim_3_out_46,
       decodeur_sim_3_out_47, decodeur_sim_3_out_48, decodeur_sim_3_out_49, decodeur_sim_3_out_50,
       decodeur_sim_3_out_51, decodeur_sim_3_out_52, decodeur_sim_3_out_53, decodeur_sim_3_out_54,
       decodeur_sim_3_out_55, decodeur_sim_3_out_56, decodeur_sim_3_out_57, decodeur_sim_3_out_58,
       decodeur_sim_3_out_59, decodeur_sim_3_out_60, decodeur_sim_3_out_61, decodeur_sim_3_out_62,
       decodeur_sim_3_out_63, decodeur_sim_3_out_64, decodeur_sim_3_out_65, decodeur_sim_3_out_66;

  Clock clock_1 (.out(clock_1_out));
  Clock #(.lowDuration(2)) clock_2 (.out(clock_2_out));
  Generateur_sinus sinus_fast (.in_1(clock_1_out), .out_2(sinus_fast_out_2));
  Generateur_sinus sinus_slow (.in_1(clock_2_out), .out_2(sinus_slow_out_2));
  not not_1 (not_1_out[7], sinus_fast_out_2[7]);
  not not_2 (not_2_out[7], sinus_slow_out_2[7]);
  Clock #(.highDuration(4), .lowDuration(4)) sample_clk (.out(sample_clk_out));
  DotMatrix #(.matrixcols(64), .matrixrows(32)) dotmatrix_1 (
    .col0(decodeur_sim_1_out_3), .col1(decodeur_sim_1_out_4), .col2(decodeur_sim_1_out_5),
    .col3(decodeur_sim_1_out_6), .col4(decodeur_sim_1_out_7), .col5(decodeur_sim_1_out_8),
    .col6(decodeur_sim_1_out_9), .col7(decodeur_sim_1_out_10), .col8(decodeur_sim_1_out_11),
    .col9(decodeur_sim_1_out_12), .col10(decodeur_sim_1_out_13), .col11(decodeur_sim_1_out_14),
    .col12(decodeur_sim_1_out_15), .col13(decodeur_sim_1_out_16), .col14(decodeur_sim_1_out_17),
    .col15(decodeur_sim_1_out_18), .col16(decodeur_sim_1_out_19), .col17(decodeur_sim_1_out_20),
    .col18(decodeur_sim_1_out_21), .col19(decodeur_sim_1_out_22), .col20(decodeur_sim_1_out_23),
    .col21(decodeur_sim_1_out_24), .col22(decodeur_sim_1_out_25), .col23(decodeur_sim_1_out_26),
    .col24(decodeur_sim_1_out_27), .col25(decodeur_sim_1_out_28), .col26(decodeur_sim_1_out_29),
    .col27(decodeur_sim_1_out_30), .col28(decodeur_sim_1_out_31), .col29(decodeur_sim_1_out_32),
    .col30(decodeur_sim_1_out_33), .col31(decodeur_sim_1_out_34), .col32(decodeur_sim_1_out_35),
    .col33(decodeur_sim_1_out_36), .col34(decodeur_sim_1_out_37), .col35(decodeur_sim_1_out_38),
    .col36(decodeur_sim_1_out_39), .col37(decodeur_sim_1_out_40), .col38(decodeur_sim_1_out_41),
    .col39(decodeur_sim_1_out_42), .col40(decodeur_sim_1_out_43), .col41(decodeur_sim_1_out_44),
    .col42(decodeur_sim_1_out_45), .col43(decodeur_sim_1_out_46), .col44(decodeur_sim_1_out_47),
    .col45(decodeur_sim_1_out_48), .col46(decodeur_sim_1_out_49), .col47(decodeur_sim_1_out_50),
    .col48(decodeur_sim_1_out_51), .col49(decodeur_sim_1_out_52), .col50(decodeur_sim_1_out_53),
    .col51(decodeur_sim_1_out_54), .col52(decodeur_sim_1_out_55), .col53(decodeur_sim_1_out_56),
    .col54(decodeur_sim_1_out_57), .col55(decodeur_sim_1_out_58), .col56(decodeur_sim_1_out_59),
    .col57(decodeur_sim_1_out_60), .col58(decodeur_sim_1_out_61), .col59(decodeur_sim_1_out_62),
    .col60(decodeur_sim_1_out_63), .col61(decodeur_sim_1_out_64), .col62(decodeur_sim_1_out_65),
    .col63(decodeur_sim_1_out_66));
  Decodeur_sim decodeur_sim_1 (
    .clk(sample_clk_out), .in_2(sinus_fast_out_2[7:3]), .out_3(decodeur_sim_1_out_3),
    .out_4(decodeur_sim_1_out_4), .out_5(decodeur_sim_1_out_5), .out_6(decodeur_sim_1_out_6),
    .out_7(decodeur_sim_1_out_7), .out_8(decodeur_sim_1_out_8), .out_9(decodeur_sim_1_out_9),
    .out_10(decodeur_sim_1_out_10), .out_11(decodeur_sim_1_out_11), .out_12(decodeur_sim_1_out_12),
    .out_13(decodeur_sim_1_out_13), .out_14(decodeur_sim_1_out_14), .out_15(decodeur_sim_1_out_15),
    .out_16(decodeur_sim_1_out_16), .out_17(decodeur_sim_1_out_17), .out_18(decodeur_sim_1_out_18),
    .out_19(decodeur_sim_1_out_19), .out_20(decodeur_sim_1_out_20), .out_21(decodeur_sim_1_out_21),
    .out_22(decodeur_sim_1_out_22), .out_23(decodeur_sim_1_out_23), .out_24(decodeur_sim_1_out_24),
    .out_25(decodeur_sim_1_out_25), .out_26(decodeur_sim_1_out_26), .out_27(decodeur_sim_1_out_27),
    .out_28(decodeur_sim_1_out_28), .out_29(decodeur_sim_1_out_29), .out_30(decodeur_sim_1_out_30),
    .out_31(decodeur_sim_1_out_31), .out_32(decodeur_sim_1_out_32), .out_33(decodeur_sim_1_out_33),
    .out_34(decodeur_sim_1_out_34), .out_35(decodeur_sim_1_out_35), .out_36(decodeur_sim_1_out_36),
    .out_37(decodeur_sim_1_out_37), .out_38(decodeur_sim_1_out_38), .out_39(decodeur_sim_1_out_39),
    .out_40(decodeur_sim_1_out_40), .out_41(decodeur_sim_1_out_41), .out_42(decodeur_sim_1_out_42),
    .out_43(decodeur_sim_1_out_43), .out_44(decodeur_sim_1_out_44), .out_45(decodeur_sim_1_out_45),
    .out_46(decodeur_sim_1_out_46), .out_47(decodeur_sim_1_out_47), .out_48(decodeur_sim_1_out_48),
    .out_49(decodeur_sim_1_out_49), .out_50(decodeur_sim_1_out_50), .out_51(decodeur_sim_1_out_51),
    .out_52(decodeur_sim_1_out_52), .out_53(decodeur_sim_1_out_53), .out_54(decodeur_sim_1_out_54),
    .out_55(decodeur_sim_1_out_55), .out_56(decodeur_sim_1_out_56), .out_57(decodeur_sim_1_out_57),
    .out_58(decodeur_sim_1_out_58), .out_59(decodeur_sim_1_out_59), .out_60(decodeur_sim_1_out_60),
    .out_61(decodeur_sim_1_out_61), .out_62(decodeur_sim_1_out_62), .out_63(decodeur_sim_1_out_63),
    .out_64(decodeur_sim_1_out_64), .out_65(decodeur_sim_1_out_65), .out_66(decodeur_sim_1_out_66));
  Clock #(.highDuration(4), .lowDuration(4)) clock_3 (.out(clock_3_out));
  DotMatrix #(.matrixcols(64), .matrixrows(32)) dotmatrix_2 (
    .col0(decodeur_sim_2_out_3), .col1(decodeur_sim_2_out_4), .col2(decodeur_sim_2_out_5),
    .col3(decodeur_sim_2_out_6), .col4(decodeur_sim_2_out_7), .col5(decodeur_sim_2_out_8),
    .col6(decodeur_sim_2_out_9), .col7(decodeur_sim_2_out_10), .col8(decodeur_sim_2_out_11),
    .col9(decodeur_sim_2_out_12), .col10(decodeur_sim_2_out_13), .col11(decodeur_sim_2_out_14),
    .col12(decodeur_sim_2_out_15), .col13(decodeur_sim_2_out_16), .col14(decodeur_sim_2_out_17),
    .col15(decodeur_sim_2_out_18), .col16(decodeur_sim_2_out_19), .col17(decodeur_sim_2_out_20),
    .col18(decodeur_sim_2_out_21), .col19(decodeur_sim_2_out_22), .col20(decodeur_sim_2_out_23),
    .col21(decodeur_sim_2_out_24), .col22(decodeur_sim_2_out_25), .col23(decodeur_sim_2_out_26),
    .col24(decodeur_sim_2_out_27), .col25(decodeur_sim_2_out_28), .col26(decodeur_sim_2_out_29),
    .col27(decodeur_sim_2_out_30), .col28(decodeur_sim_2_out_31), .col29(decodeur_sim_2_out_32),
    .col30(decodeur_sim_2_out_33), .col31(decodeur_sim_2_out_34), .col32(decodeur_sim_2_out_35),
    .col33(decodeur_sim_2_out_36), .col34(decodeur_sim_2_out_37), .col35(decodeur_sim_2_out_38),
    .col36(decodeur_sim_2_out_39), .col37(decodeur_sim_2_out_40), .col38(decodeur_sim_2_out_41),
    .col39(decodeur_sim_2_out_42), .col40(decodeur_sim_2_out_43), .col41(decodeur_sim_2_out_44),
    .col42(decodeur_sim_2_out_45), .col43(decodeur_sim_2_out_46), .col44(decodeur_sim_2_out_47),
    .col45(decodeur_sim_2_out_48), .col46(decodeur_sim_2_out_49), .col47(decodeur_sim_2_out_50),
    .col48(decodeur_sim_2_out_51), .col49(decodeur_sim_2_out_52), .col50(decodeur_sim_2_out_53),
    .col51(decodeur_sim_2_out_54), .col52(decodeur_sim_2_out_55), .col53(decodeur_sim_2_out_56),
    .col54(decodeur_sim_2_out_57), .col55(decodeur_sim_2_out_58), .col56(decodeur_sim_2_out_59),
    .col57(decodeur_sim_2_out_60), .col58(decodeur_sim_2_out_61), .col59(decodeur_sim_2_out_62),
    .col60(decodeur_sim_2_out_63), .col61(decodeur_sim_2_out_64), .col62(decodeur_sim_2_out_65),
    .col63(decodeur_sim_2_out_66));
  Decodeur_sim decodeur_sim_2 (
    .clk(clock_3_out), .in_2(sinus_slow_out_2[7:3]), .out_3(decodeur_sim_2_out_3),
    .out_4(decodeur_sim_2_out_4), .out_5(decodeur_sim_2_out_5), .out_6(decodeur_sim_2_out_6),
    .out_7(decodeur_sim_2_out_7), .out_8(decodeur_sim_2_out_8), .out_9(decodeur_sim_2_out_9),
    .out_10(decodeur_sim_2_out_10), .out_11(decodeur_sim_2_out_11), .out_12(decodeur_sim_2_out_12),
    .out_13(decodeur_sim_2_out_13), .out_14(decodeur_sim_2_out_14), .out_15(decodeur_sim_2_out_15),
    .out_16(decodeur_sim_2_out_16), .out_17(decodeur_sim_2_out_17), .out_18(decodeur_sim_2_out_18),
    .out_19(decodeur_sim_2_out_19), .out_20(decodeur_sim_2_out_20), .out_21(decodeur_sim_2_out_21),
    .out_22(decodeur_sim_2_out_22), .out_23(decodeur_sim_2_out_23), .out_24(decodeur_sim_2_out_24),
    .out_25(decodeur_sim_2_out_25), .out_26(decodeur_sim_2_out_26), .out_27(decodeur_sim_2_out_27),
    .out_28(decodeur_sim_2_out_28), .out_29(decodeur_sim_2_out_29), .out_30(decodeur_sim_2_out_30),
    .out_31(decodeur_sim_2_out_31), .out_32(decodeur_sim_2_out_32), .out_33(decodeur_sim_2_out_33),
    .out_34(decodeur_sim_2_out_34), .out_35(decodeur_sim_2_out_35), .out_36(decodeur_sim_2_out_36),
    .out_37(decodeur_sim_2_out_37), .out_38(decodeur_sim_2_out_38), .out_39(decodeur_sim_2_out_39),
    .out_40(decodeur_sim_2_out_40), .out_41(decodeur_sim_2_out_41), .out_42(decodeur_sim_2_out_42),
    .out_43(decodeur_sim_2_out_43), .out_44(decodeur_sim_2_out_44), .out_45(decodeur_sim_2_out_45),
    .out_46(decodeur_sim_2_out_46), .out_47(decodeur_sim_2_out_47), .out_48(decodeur_sim_2_out_48),
    .out_49(decodeur_sim_2_out_49), .out_50(decodeur_sim_2_out_50), .out_51(decodeur_sim_2_out_51),
    .out_52(decodeur_sim_2_out_52), .out_53(decodeur_sim_2_out_53), .out_54(decodeur_sim_2_out_54),
    .out_55(decodeur_sim_2_out_55), .out_56(decodeur_sim_2_out_56), .out_57(decodeur_sim_2_out_57),
    .out_58(decodeur_sim_2_out_58), .out_59(decodeur_sim_2_out_59), .out_60(decodeur_sim_2_out_60),
    .out_61(decodeur_sim_2_out_61), .out_62(decodeur_sim_2_out_62), .out_63(decodeur_sim_2_out_63),
    .out_64(decodeur_sim_2_out_64), .out_65(decodeur_sim_2_out_65), .out_66(decodeur_sim_2_out_66));
  // DipSwitch #(.number(2)) Control_A: pin names not known
  // Probe on {not_1_out[7], sinus_fast_out_2[6:0]}
  // DipSwitch #(.number(2)) dipswitch_1: pin names not known
  mixer mixer_1 (
    .Control_A(undriven), .Canal_A({not_1_out[7], sinus_fast_out_2[6:0]}), .Control_B(undriven_2),
    .Canal_B({not_2_out[7], sinus_slow_out_2[6:0]}), .Audio_out({mixer_1_audio_out[7], mixer_1_audio_out_2}));
  // Probe on {mixer_1_audio_out[7], mixer_1_audio_out_2}
  Clock #(.highDuration(4), .lowDuration(4)) clock_4 (.out(clock_4_out));
  not not_3 (not_3_out[7], mixer_1_audio_out[7]);
  DotMatrix #(.matrixcols(64), .matrixrows(32)) dotmatrix_3 (
    .col0(decodeur_sim_3_out_3), .col1(decodeur_sim_3_out_4), .col2(decodeur_sim_3_out_5),
    .col3(decodeur_sim_3_out_6), .col4(decodeur_sim_3_out_7), .col5(decodeur_sim_3_out_8),
    .col6(decodeur_sim_3_out_9), .col7(decodeur_sim_3_out_10), .col8(decodeur_sim_3_out_11),
    .col9(decodeur_sim_3_out_12), .col10(decodeur_sim_3_out_13), .col11(decodeur_sim_3_out_14),
    .col12(decodeur_sim_3_out_15), .col13(decodeur_sim_3_out_16), .col14(decodeur_sim_3_out_17),
    .col15(decodeur_sim_3_out_18), .col16(decodeur_sim_3_out_19), .col17(decodeur_sim_3_out_20),
    .col18(decodeur_sim_3_out_21), .col19(decodeur_sim_3_out_22), .col20(decodeur_sim_3_out_23),
    .col21(decodeur_sim_3_out_24), .col22(decodeur_sim_3_out_25), .col23(decodeur_sim_3_out_26),
    .col24(decodeur_sim_3_out_27), .col25(decodeur_sim_3_out_28), .col26(decodeur_sim_3_out_29),
    .col27(decodeur_sim_3_out_30), .col28(decodeur_sim_3_out_31), .col29(decodeur_sim_3_out_32),
    .col30(decodeur_sim_3_out_33), .col31(decodeur_sim_3_out_34), .col32(decodeur_sim_3_out_35),
    .col33(decodeur_sim_3_out_36), .col34(decodeur_sim_3_out_37), .col35(decodeur_sim_3_out_38),
    .col36(decodeur_sim_3_out_39), .col37(decodeur_sim_3_out_40), .col38(decodeur_sim_3_out_41),
    .col39(decodeur_sim_3_out_42), .col40(decodeur_sim_3_out_43), .col41(decodeur_sim_3_out_44),
    .col42(decodeur_sim_3_out_45), .col43(decodeur_sim_3_out_46), .col44(decodeur_sim_3_out_47),
    .col45(decodeur_sim_3_out_48), .col46(decodeur_sim_3_out_49), .col47(decodeur_sim_3_out_50),
    .col48(decodeur_sim_3_out_51), .col49(decodeur_sim_3_out_52), .col50(decodeur_sim_3_out_53),
    .col51(decodeur_sim_3_out_54), .col52(decodeur_sim_3_out_55), .col53(decodeur_sim_3_out_56),
    .col54(decodeur_sim_3_out_57), .col55(decodeur_sim_3_out_58), .col56(decodeur_sim_3_out_59),
    .col57(decodeur_sim_3_out_60), .col58(decodeur_sim_3_out_61), .col59(decodeur_sim_3_out_62),
    .col60(decodeur_sim_3_out_63), .col61(decodeur_sim_3_out_64), .col62(decodeur_sim_3_out_65),
    .col63(decodeur_sim_3_out_66));
  Decodeur_sim decodeur_sim_3 (
    .clk(clock_4_out), .in_2({not_3_out[7], mixer_1_audio_out_2[6:3]}), .out_3(decodeur_sim_3_out_3),
    .out_4(decodeur_sim_3_out_4), .out_5(decodeur_sim_3_out_5), .out_6(decodeur_sim_3_out_6),
    .out_7(decodeur_sim_3_out_7), .out_8(decodeur_sim_3_out_8), .out_9(decodeur_sim_3_out_9),
    .out_10(decodeur_sim_3_out_10), .out_11(decodeur_sim_3_out_11), .out_12(decodeur_sim_3_out_12),
    .out_13(decodeur_sim_3_out_13), .out_14(decodeur_sim_3_out_14), .out_15(decodeur_sim_3_out_15),
    .out_16(decodeur_sim_3_out_16), .out_17(decodeur_sim_3_out_17), .out_18(decodeur_sim_3_out_18),
    .out_19(decodeur_sim_3_out_19), .out_20(decodeur_sim_3_out_20), .out_21(decodeur_sim_3_out_21),
    .out_22(decodeur_sim_3_out_22), .out_23(decodeur_sim_3_out_23), .out_24(decodeur_sim_3_out_24),
    .out_25(decodeur_sim_3_out_25), .out_26(decodeur_sim_3_out_26), .out_27(decodeur_sim_3_out_27),
    .out_28(decodeur_sim_3_out_28), .out_29(decodeur_sim_3_out_29), .out_30(decodeur_sim_3_out_30),
    .out_31(decodeur_sim_3_out_31), .out_32(decodeur_sim_3_out_32), .out_33(decodeur_sim_3_out_33),
    .out_34(decodeur_sim_3_out_34), .out_35(decodeur_sim_3_out_35), .out_36(decodeur_sim_3_out_36),
    .out_37(decodeur_sim_3_out_37), .out_38(decodeur_sim_3_out_38), .out_39(decodeur_sim_3_out_39),
    .out_40(decodeur_sim_3_out_40), .out_41(decodeur_sim_3_out_41), .out_42(decodeur_sim_3_out_42),
    .out_43(decodeur_sim_3_out_43), .out_44(decodeur_sim_3_out_44), .out_45(decodeur_sim_3_out_45),
    .out_46(decodeur_sim_3_out_46), .out_47(decodeur_sim_3_out_47), .out_48(decodeur_sim_3_out_48),
    .out_49(decodeur_sim_3_out_49), .out_50(decodeur_sim_3_out_50), .out_51(decodeur_sim_3_out_51),
    .out_52(decodeur_sim_3_out_52), .out_53(decodeur_sim_3_out_53), .out_54(decodeur_sim_3_out_54),
    .out_55(decodeur_sim_3_out_55), .out_56(decodeur_sim_3_out_56), .out_57(decodeur_sim_3_out_57),
    .out_58(decodeur_sim_3_out_58), .out_59(decodeur_sim_3_out_59), .out_60(decodeur_sim_3_out_60),
    .out_61(decodeur_sim_3_out_61), .out_62(decodeur_sim_3_out_62), .out_63(decodeur_sim_3_out_63),
    .out_64(decodeur_sim_3_out_64), .out_65(decodeur_sim_3_out_65), .out_66(decodeur_sim_3_out_66));

  // Notes on the sheet:
  //   Canal A
  //   Canal B
  //   Circuit de test. Ne modifiez pas ce circuit!!!!
  //   modifiez seulement le bloc appelé mixer pour y metre votre tablée de mixage
  //   Sortie
endmodule

module Decodeur_sim (
  input  clk,
  input  [4:0] in_2,
  output [31:0] out_3,
  output [31:0] out_4,
  output [31:0] out_5,
  output [31:0] out_6,
  output [31:0] out_7,
  output [31:0] out_8,
  output [31:0] out_9,
  output [31:0] out_10,
  output [31:0] out_11,
  output [31:0] out_12,
  output [31:0] out_13,
  output [31:0] out_14,
  output [31:0] out_15,
  output [31:0] out_16,
  output [31:0] out_17,
  output [31:0] out_18,
  output [31:0] out_19,
  output [31:0] out_20,
  output [31:0] out_21,
  output [31:0] out_22,
  output [31:0] out_23,
  output [31:0] out_24,
  output [31:0] out_25,
  output [31:0] out_26,
  output [31:0] out_27,
  output [31:0] out_28,
  output [31:0] out_29,
  output [31:0] out_30,
  output [31:0] out_31,
  output [31:0] out_32,
  output [31:0] out_33,
  output [31:0] out_34,
  output [31:0] out_35,
  output [31:0] out_36,
  output [31:0] out_37,
  output [31:0] out_38,
  output [31:0] out_39,
  output [31:0] out_40,
  output [31:0] out_41,
  output [31:0] out_42,
  output [31:0] out_43,
  output [31:0] out_44,
  output [31:0] out_45,
  output [31:0] out_46,
  output [31:0] out_47,
  output [31:0] out_48,
  output [31:0] out_49,
  output [31:0] out_50,
  output [31:0] out_51,
  output [31:0] out_52,
  output [31:0] out_53,
  output [31:0] out_54,
  output [31:0] out_55,
  output [31:0] out_56,
  output [31:0] out_57,
  output [31:0] out_58,
  output [31:0] out_59,
  output [31:0] out_60,
  output [31:0] out_61,
  output [31:0] out_62,
  output [31:0] out_63,
  output [31:0] out_64,
  output [31:0] out_65,
  output [31:0] out_66
);

  wire [31:0] decoder_1_out0;

  Decoder #(.select(5)) decoder_1 (
    .out0(decoder_1_out0[0]), .out1(decoder_1_out0[1]), .out2(decoder_1_out0[2]), .out3(decoder_1_out0[3]),
    .out4(decoder_1_out0[4]), .out5(decoder_1_out0[5]), .out6(decoder_1_out0[6]), .out7(decoder_1_out0[7]),
    .out8(decoder_1_out0[8]), .out9(decoder_1_out0[9]), .out10(decoder_1_out0[10]),
    .out11(decoder_1_out0[11]), .out12(decoder_1_out0[12]), .out13(decoder_1_out0[13]),
    .out14(decoder_1_out0[14]), .out15(decoder_1_out0[15]), .out16(decoder_1_out0[16]),
    .out17(decoder_1_out0[17]), .out18(decoder_1_out0[18]), .out19(decoder_1_out0[19]),
    .out20(decoder_1_out0[20]), .out21(decoder_1_out0[21]), .out22(decoder_1_out0[22]),
    .out23(decoder_1_out0[23]), .out24(decoder_1_out0[24]), .out25(decoder_1_out0[25]),
    .out26(decoder_1_out0[26]), .out27(decoder_1_out0[27]), .out28(decoder_1_out0[28]),
    .out29(decoder_1_out0[29]), .out30(decoder_1_out0[30]), .out31(decoder_1_out0[31]), .sel(in_2));  // open: en
  Register #(.width(32)) register_1 (.D(decoder_1_out0), .clk(clk), .Q(out_3));  // open: en, clr
  Register #(.width(32)) register_2 (.D(out_3), .clk(clk), .Q(out_4));  // open: en, clr
  Register #(.width(32)) register_3 (.D(out_4), .clk(clk), .Q(out_5));  // open: en, clr
  Register #(.width(32)) register_4 (.D(out_5), .clk(clk), .Q(out_6));  // open: en, clr
  Register #(.width(32)) register_5 (.D(out_6), .clk(clk), .Q(out_7));  // open: en, clr
  Register #(.width(32)) register_6 (.D(out_7), .clk(clk), .Q(out_8));  // open: en, clr
  Register #(.width(32)) register_7 (.D(out_8), .clk(clk), .Q(out_9));  // open: en, clr
  Register #(.width(32)) register_8 (.D(out_9), .clk(clk), .Q(out_10));  // open: en, clr
  Register #(.width(32)) register_9 (.D(out_10), .clk(clk), .Q(out_11));  // open: en, clr
  Register #(.width(32)) register_10 (.D(out_11), .clk(clk), .Q(out_12));  // open: en, clr
  Register #(.width(32)) register_11 (.D(out_12), .clk(clk), .Q(out_13));  // open: en, clr
  Register #(.width(32)) register_12 (.D(out_13), .clk(clk), .Q(out_14));  // open: en, clr
  Register #(.width(32)) register_13 (.D(out_14), .clk(clk), .Q(out_15));  // open: en, clr
  Register #(.width(32)) register_14 (.D(out_15), .clk(clk), .Q(out_16));  // open: en, clr
  Register #(.width(32)) register_15 (.D(out_16), .clk(clk), .Q(out_17));  // open: en, clr
  Register #(.width(32)) register_16 (.D(out_17), .clk(clk), .Q(out_18));  // open: en, clr
  Register #(.width(32)) register_17 (.D(out_18), .clk(clk), .Q(out_19));  // open: en, clr
  Register #(.width(32)) register_18 (.D(out_19), .clk(clk), .Q(out_20));  // open: en, clr
  Register #(.width(32)) register_19 (.D(out_20), .clk(clk), .Q(out_21));  // open: en, clr
  Register #(.width(32)) register_20 (.D(out_21), .clk(clk), .Q(out_22));  // open: en, clr
  Register #(.width(32)) register_21 (.D(out_22), .clk(clk), .Q(out_23));  // open: en, clr
  Register #(.width(32)) register_22 (.D(out_23), .clk(clk), .Q(out_24));  // open: en, clr
  Register #(.width(32)) register_23 (.D(out_24), .clk(clk), .Q(out_25));  // open: en, clr
  Register #(.width(32)) register_24 (.D(out_25), .clk(clk), .Q(out_26));  // open: en, clr
  Register #(.width(32)) register_25 (.D(out_26), .clk(clk), .Q(out_27));  // open: en, clr
  Register #(.width(32)) register_26 (.D(out_27), .clk(clk), .Q(out_28));  // open: en, clr
  Register #(.width(32)) register_27 (.D(out_28), .clk(clk), .Q(out_29));  // open: en, clr
  Register #(.width(32)) register_28 (.D(out_29), .clk(clk), .Q(out_30));  // open: en, clr
  Register #(.width(32)) register_29 (.D(out_30), .clk(clk), .Q(out_31));  // open: en, clr
  Register #(.width(32)) register_30 (.D(out_31), .clk(clk), .Q(out_32));  // open: en, clr
  Register #(.width(32)) register_31 (.D(out_32), .clk(clk), .Q(out_33));  // open: en, clr
  Register #(.width(32)) register_32 (.D(out_33), .clk(clk), .Q(out_34));  // open: en, clr
  Register #(.width(32)) register_33 (.D(out_34), .clk(clk), .Q(out_35));  // open: en, clr
  Register #(.width(32)) register_34 (.D(out_35), .clk(clk), .Q(out_36));  // open: en, clr
  Register #(.width(32)) register_35 (.D(out_36), .clk(clk), .Q(out_37));  // open: en, clr
  Register #(.width(32)) register_36 (.D(out_37), .clk(clk), .Q(out_38));  // open: en, clr
  Register #(.width(32)) register_37 (.D(out_38), .clk(clk), .Q(out_39));  // open: en, clr
  Register #(.width(32)) register_38 (.D(out_39), .clk(clk), .Q(out_40));  // open: en, clr
  Register #(.width(32)) register_39 (.D(out_40), .clk(clk), .Q(out_41));  // open: en, clr
  Register #(.width(32)) register_40 (.D(out_41), .clk(clk), .Q(out_42));  // open: en, clr
  Register #(.width(32)) register_41 (.D(out_42), .clk(clk), .Q(out_43));  // open: en, clr
  Register #(.width(32)) register_42 (.D(out_43), .clk(clk), .Q(out_44));  // open: en, clr
  Register #(.width(32)) register_43 (.D(out_44), .clk(clk), .Q(out_45));  // open: en, clr
  Register #(.width(32)) register_44 (.D(out_45), .clk(clk), .Q(out_46));  // open: en, clr
  Register #(.width(32)) register_45 (.D(out_46), .clk(clk), .Q(out_47));  // open: en, clr
  Register #(.width(32)) register_46 (.D(out_47), .clk(clk), .Q(out_48));  // open: en, clr
  Register #(.width(32)) register_47 (.D(out_48), .clk(clk), .Q(out_49));  // open: en, clr
  Register #(.width(32)) register_48 (.D(out_49), .clk(clk), .Q(out_50));  // open: en, clr
  Register #(.width(32)) register_49 (.D(out_50), .clk(clk), .Q(out_51));  // open: en, clr
  Register #(.width(32)) register_50 (.D(out_51), .clk(clk), .Q(out_52));  // open: en, clr
  Register #(.width(32)) register_51 (.D(out_52), .clk(clk), .Q(out_53));  // open: en, clr
  Register #(.width(32)) register_52 (.D(out_53), .clk(clk), .Q(out_54));  // open: en, clr
  Register #(.width(32)) register_53 (.D(out_54), .clk(clk), .Q(out_55));  // open: en, clr
  Register #(.width(32)) register_54 (.D(out_55), .clk(clk), .Q(out_56));  // open: en, clr
  Register #(.width(32)) register_55 (.D(out_56), .clk(clk), .Q(out_57));  // open: en, clr
  Register #(.width(32)) register_56 (.D(out_57), .clk(clk), .Q(out_58));  // open: en, clr
  Register #(.width(32)) register_57 (.D(out_58), .clk(clk), .Q(out_59));  // open: en, clr
  Register #(.width(32)) register_58 (.D(out_59), .clk(clk), .Q(out_60));  // open: en, clr
  Register #(.width(32)) register_59 (.D(out_60), .clk(clk), .Q(out_61));  // open: en, clr
  Register #(.width(32)) register_60 (.D(out_61), .clk(clk), .Q(out_62));  // open: en, clr
  Register #(.width(32)) register_61 (.D(out_62), .clk(clk), .Q(out_63));  // open: en, clr
  Register #(.width(32)) register_62 (.D(out_63), .clk(clk), .Q(out_64));  // open: en, clr
  Register #(.width(32)) register_63 (.D(out_64), .clk(clk), .Q(out_65));  // open: en, clr
  Register #(.width(32)) register_64 (.D(out_65), .clk(clk), .Q(out_66));  // open: en, clr

  // Notes on the sheet:
  //   Circuit de test. Ne modifiez pas ce circuit!!!!
endmodule

module Generateur_sinus (
  input  in_1,
  output [7:0] out_2
);

  wire [7:0] counter_1_q, rom_1_data;
  wire [7:7] multiplier_1_out, not_1_out;

  Counter counter_1 (.clk(in_1), .Q(counter_1_q));  // open: clr, load, up, count, D, carry
  ROM rom_1 (.addr(counter_1_q), .data(rom_1_data));
  not not_1 (not_1_out[7], rom_1_data[7]);
  not not_2 (out_2[7], multiplier_1_out[7]);
  Multiplier multiplier_1 (
    .a({{2{not_1_out[7]}}, rom_1_data[6:1]}), .b(8'h3), .out({multiplier_1_out[7], out_2[6:0]}));  // open: cin, cout

  // Notes on the sheet:
  //   contents of rom_1 (hex, n*v repeats v):
  //   80 82 83 85 86 88 89 8b 8c 8e 8f 91 92 94 95 97 98 9a 9b 9c 9e 9f a1 a2 a3 a4 a6 a7 a8 a9 aa ac ad
  //   ae af b0 b1 b2 b3 b4 b5 b5 b6 b7 b8 b8 b9 ba ba bb bb bc bc bd bd 4*be 10*bf 4*be bd bd bd bc bc bb
  //   bb ba b9 b9 b8 b7 b7 b6 b5 b4 b3 b2 b1 b0 af ae ad ac ab aa a9 a7 a6 a5 a4 a2 a1 a0 9e 9d 9c 9a 99
  //   97 96 95 93 92 90 8f 8d 8c 8a 89 87 85 84 82 81 7f 7e 7c 7b 79 77 76 74 73 71 70 6e 6d 6b 6a 69 67
  //   66 64 63 62 60 5f 5e 5c 5b 5a 59 57 56 55 54 53 52 51 50 4f 4e 4d 4c 4b 4a 49 49 48 47 47 46 45 45
  //   44 44 43 43 43 4*42 10*41 4*42 43 43 44 44 45 45 46 46 47 48 48 49 4a 4b 4b 4c 4d 4e 4f 50 51 52 53
  //   54 56 57 58 59 5a 5c 5d 5e 5f 61 62 64 65 66 68 69 6b 6c 6e 6f 71 72 74 75 77 78 7a 7b 7d 7e 80
  //   Circuit de test. Ne modifiez pas ce circuit!!!!
endmodule

module mixer (
  input  [1:0] Control_A,
  input  [7:0] Canal_A,
  input  [1:0] Control_B,
  input  [7:0] Canal_B,
  output [7:0] Audio_out
);

  wire alucomplexe8bit_1_n_out, alucomplexe8bit_1_v_out, alucomplexe8bit_2_n_out, alucomplexe8bit_2_v_out,
       alucomplexe8bit_3_n_out, alucomplexe8bit_3_v_out;
  wire [1:0] laisserpasser_1_f, overflowhandler2bit_1_vn_out, overflowhandler2bit_2_vn_out,
       overflowhandler2bit_3_vn_out;
  wire [2:0] controldecoder_1_ctrl_out, controldecoder_2_ctrl_out;
  wire [7:0] A_Normalizer, alucomplexe8bit_1_res, alucomplexe8bit_2_res, alucomplexe8bit_3_res, B_Normalizer,
       multiplexer_3_out, multiplexer_4_out;

  ControlDecoder controldecoder_1 (.Ctrl_in(Control_A), .Ctrl_out(controldecoder_1_ctrl_out));
  ControlDecoder controldecoder_2 (.Ctrl_in(Control_B), .Ctrl_out(controldecoder_2_ctrl_out));
  Multiplexer #(.width(8)) multiplexer_1 (
    .in0({8{1'b0}}), .in1(Canal_A), .out(A_Normalizer), .sel(controldecoder_1_ctrl_out[0]));
  Multiplexer #(.width(8)) multiplexer_2 (
    .in0({8{1'b0}}), .in1(Canal_B), .out(B_Normalizer), .sel(controldecoder_2_ctrl_out[0]));
  AluComplexe8Bit alucomplexe8bit_1 (
    .OP(controldecoder_1_ctrl_out), .A(Canal_A), .B(A_Normalizer), .V_Out(alucomplexe8bit_1_v_out),
    .Res(alucomplexe8bit_1_res), .N_out(alucomplexe8bit_1_n_out));  // open: C_out, Z_out
  AluComplexe8Bit alucomplexe8bit_2 (
    .OP(controldecoder_2_ctrl_out), .A(Canal_B), .B(B_Normalizer), .V_Out(alucomplexe8bit_2_v_out),
    .Res(alucomplexe8bit_2_res), .N_out(alucomplexe8bit_2_n_out));  // open: C_out, Z_out
  Multiplexer #(.select(2), .width(8)) multiplexer_3 (
    .in0(alucomplexe8bit_1_res), .in1(alucomplexe8bit_1_res), .in2(8'h80), .in3(8'h7f),
    .out(multiplexer_3_out), .sel({overflowhandler2bit_1_vn_out[0], overflowhandler2bit_1_vn_out[1]}));
  Multiplexer #(.select(2), .width(8)) multiplexer_4 (
    .in0(alucomplexe8bit_1_res), .in1(alucomplexe8bit_1_res), .in2(8'h80), .in3(8'h7f),
    .out(multiplexer_4_out), .sel({overflowhandler2bit_2_vn_out[0], overflowhandler2bit_2_vn_out[1]}));
  OverflowHandler2Bit overflowhandler2bit_1 (
    .V(alucomplexe8bit_1_v_out), .N(alucomplexe8bit_1_n_out),
    .VN_Out({overflowhandler2bit_1_vn_out[0], overflowhandler2bit_1_vn_out[1]}));
  OverflowHandler2Bit overflowhandler2bit_2 (
    .V(alucomplexe8bit_2_v_out), .N(alucomplexe8bit_2_n_out),
    .VN_Out({overflowhandler2bit_2_vn_out[0], overflowhandler2bit_2_vn_out[1]}));
  AluComplexe8Bit alucomplexe8bit_3 (
    .OP(3'b000), .A(multiplexer_3_out), .B(multiplexer_4_out), .V_Out(alucomplexe8bit_3_v_out),
    .Res(alucomplexe8bit_3_res), .N_out(alucomplexe8bit_3_n_out));  // open: C_out, Z_out
  OverflowHandler2Bit overflowhandler2bit_3 (
    .V(alucomplexe8bit_3_v_out), .N(alucomplexe8bit_3_n_out), .VN_Out(overflowhandler2bit_3_vn_out));
  LaisserPasser laisserpasser_1 (
    .A(overflowhandler2bit_1_vn_out), .R({overflowhandler2bit_3_vn_out[0], overflowhandler2bit_3_vn_out[1]}),
    .B(overflowhandler2bit_2_vn_out), .F(laisserpasser_1_f));
  Multiplexer #(.select(2), .width(8)) multiplexer_5 (
    .in0(8'h80), .in1(8'h7f), .in3({8{1'b0}}), .out(Audio_out), .sel(laisserpasser_1_f));  // open: in2
endmodule

module Test_Carte (
  input  [7:0] SW,
  input  rst,
  input  clk,
  input  A_IN1_SDATA,
  input  A_IN2_SDATA,
  output A_IN1_SCLK,
  output A_IN1_nCS,
  output [7:0] LEDs,
  output A_OUT_DOUT,
  output A_OUT_SCLK,
  output A_OUT_MCLK,
  output A_OUT_LRCLK,
  output A_IN2_SCLK,
  output A_IN2_nCS
);

  wire speaker_done;
  wire [11:0] pmodmicrefcomp_1_data, pmodmicrefcomp_2_data;
  wire [13:6] mixer_1_p5;

  PmodMICRefComp pmodmicrefcomp_1 (
    .CLK(clk), .RST(rst), .SDATA(A_IN1_SDATA), .START(speaker_done), .SCLK(A_IN1_SCLK), .nCS(A_IN1_nCS),
    .DATA(pmodmicrefcomp_1_data));  // open: DONE
  PmodMICRefComp pmodmicrefcomp_2 (
    .CLK(clk), .RST(rst), .SDATA(A_IN2_SDATA), .START(speaker_done), .SCLK(A_IN2_SCLK), .nCS(A_IN2_nCS),
    .DATA(pmodmicrefcomp_2_data));  // open: DONE
  // mixer mixer_1: pin names not known; wires that end beside it: SW[1:0], pmodmicrefcomp_1_data[11:4], pmodmicrefcomp_2_data[11:4], SW[3:2], mixer_1_p5
  SpeakerCtrl speakerctrl_1 (
    .clk(clk), .rst(rst), .audio_in({2'b00, mixer_1_p5, {6{1'b0}}}), .Led(LEDs), .done(speaker_done),
    .SDOUT(A_OUT_DOUT), .SCLK(A_OUT_SCLK), .MCLK(A_OUT_MCLK), .LRCK(A_OUT_LRCLK));

  // Other names for the same wires on the sheet: sw_ctrl_A[1:0] = SW[1:0]; sw_ctrl_B[1:0] = SW[3:2]
endmodule

module ControlDecoder (
  input  [1:0] Ctrl_in,
  output [2:0] Ctrl_out
);

  wire not_1_out, not_2_out;

  not not_1 (not_1_out, Ctrl_in[1]);
  not not_2 (not_2_out, Ctrl_in[0]);
  and and_1 (Ctrl_out[2], Ctrl_in[1], not_2_out);
  and and_2 (Ctrl_out[1], not_1_out, Ctrl_in[0]);
  and and_3 (Ctrl_out[0], Ctrl_in[1], Ctrl_in[0]);
endmodule

module OverflowHandler2Bit (
  input  V,
  input  N,
  output [1:0] VN_Out
);

  Multiplexer #(.width(2)) multiplexer_1 (.in0(2'b00), .in1({V, N}), .out(VN_Out), .sel(V));
endmodule

module Maj (
  input  N_A,
  input  N_B,
  input  N_A_B,
  output N
);

  wire and_1_out, and_2_out, and_3_out;

  and and_1 (and_1_out, N_B, N_A_B);
  and and_2 (and_2_out, N_A, N_A_B);
  and and_3 (and_3_out, N_A, N_B);
  or or_1 (N, and_1_out, and_2_out, and_3_out);
endmodule

module LaisserPasser (
  input  [1:0] A,
  input  [1:0] R,
  input  [1:0] B,
  output [1:0] F
);

  wire and_1_out, and_2_out, and_3_out, and_4_out, and_5_out, and_6_out, and_7_out, and_8_out, and_9_out,
       and_10_out, and_11_out, and_12_out, and_13_out, and_14_out, and_15_out, and_16_out, and_17_out,
       and_18_out, and_19_out, not_1_out, not_2_out, not_3_out, not_4_out, not_5_out, not_6_out;

  not not_1 (not_1_out, A[1]);
  not not_2 (not_2_out, A[0]);
  not not_3 (not_3_out, R[1]);
  not not_4 (not_4_out, R[0]);
  not not_5 (not_5_out, B[1]);
  not not_6 (not_6_out, B[0]);
  and and_1 (and_1_out, not_2_out, not_4_out, B[1], not_6_out);
  and and_2 (and_2_out, A[1], not_2_out, not_4_out, B[1]);
  and and_3 (and_3_out, A[1], not_2_out, B[1], not_6_out);
  and and_4 (and_4_out, A[1], not_4_out, B[1], not_6_out);
  and and_5 (and_5_out, not_1_out, not_3_out, not_5_out, B[0]);
  and and_6 (and_6_out, not_1_out, not_3_out, R[0], not_5_out);
  and and_7 (and_7_out, not_3_out, R[0], not_5_out, B[0]);
  and and_8 (and_8_out, not_1_out, not_3_out, R[0], B[0]);
  and and_9 (and_9_out, not_1_out, R[0], not_5_out, B[0]);
  and and_10 (and_10_out, not_1_out, A[0], not_3_out, not_5_out);
  and and_11 (and_11_out, A[0], not_3_out, not_5_out, B[0]);
  and and_12 (and_12_out, not_1_out, A[0], not_3_out, B[0]);
  and and_13 (and_13_out, A[0], not_3_out, R[0], not_5_out);
  and and_14 (and_14_out, not_1_out, A[0], not_3_out, R[0]);
  and and_15 (and_15_out, A[0], not_3_out, R[0], B[0]);
  and and_16 (and_16_out, not_1_out, A[0], not_5_out, B[0]);
  and and_17 (and_17_out, not_1_out, A[0], R[0], not_5_out);
  and and_18 (and_18_out, A[0], R[0], not_5_out, B[0]);
  and and_19 (and_19_out, not_1_out, A[0], R[0], B[0]);
  or or_1 (F[1], and_1_out, R[1], and_2_out, and_3_out, and_4_out);
  or or_2 (F[0], and_5_out, and_6_out, and_7_out, and_8_out, and_9_out, and_10_out, and_11_out, and_12_out, and_13_out, and_14_out, and_15_out, and_16_out, and_17_out, and_18_out, and_19_out);
endmodule

// VHDL entity PmodMICRefComp, as the project stores it:
-------------------------------------------------------------------------
--    PmodMICRefComp.VHD
-------------------------------------------------------------------------
--    Author         : Ioana Dabacan
-- CopyRight 2008 Digilent Ro.
-------------------------------------------------------------------------
--    Description : This file is the VHDL code for a PmodMic controller.
--
-------------------------------------------------------------------------
--    Revision History:
-- Feb/29/2008 Created    (Ioana Dabacan)
-- Feb/29/2008 ClaudiaG : adapted for PmodMic
-- Dec/02/2023 LG (HEPIA): adapted for Basys3 (100MHz clock instead of 50)
-------------------------------------------------------------------------

library IEEE;
use IEEE.STD_LOGIC_1164.all;
use ieee.numeric_std.all;
--use IEEE.STD_LOGIC_ARITH.ALL;
--use IEEE.STD_LOGIC_UNSIGNED.ALL;

-------------------------------------------------------------------------
--Title         : AD1 controller entity
--
--    Inputs         : 5
--    Outputs        : 5
--
--    Description: This is the PmodMic controller entity. The input ports  
--                are a 100 MHz clock and an asynchronous 
--                reset button along with the data from the ADCS7476 that 
--                is serially shifted in on each clock cycle(DATA). 
--                      The outputs are the SCLK signal which clocks
--                the PmocMIC board at 12.5 MHz and a chip select 
--                signal (nCS) that enables the ADCS7476 chips on the
--                PmocMIC board as well as the 12-bit output 
--                vector labeled DATA which can be used by 
--                any external components. The START is used to tell
--                the component when to start a conversion. After a
--                conversion is done the component activates the DONE
--                signal.
--
--------------------------------------------------------------------------

entity PmodMICRefComp is
  port (
    --General usage
    CLK : in std_logic;
    RST : in std_logic;

    --Pmod interface signals
    SDATA : in  std_logic;
    SCLK  : out std_logic;
    nCS   : out std_logic;

    --User interface signals
    DATA  : out std_logic_vector(11 downto 0);
    START : in  std_logic;
    DONE  : out std_logic
    );

end PmodMICRefComp;

architecture PmodMic of PmodMICRefComp is

--------------------------------------------------------------------------------
-- Title         :     Local signal assignments
--
-- Description          : The following signals will be used to drive the  
--                            processes of this VHDL file.
--
--   current_state : This signal will be the pointer that will point at the
--                   current state of the Finite State Machine of the 
--                   controller.
--   next_state    : This signal will be the pointer that will point at the
--                   current state of the Finite State Machine of the 
--                   controller.
--   temp          : This is a 16-bit vector that will store the 16-bits of data 
--                   that are serially shifted-in form the  first ADCS7476 chip
--                   inside the PmodMIC board.
--   clk_div       : This will be the divided 12.5 MHz clock signal that will
--                   clock the PMOD-MIC board
--   clk_counter   : This counter will be used to create a divided clock signal.
--
--   shiftCounter  : This counter will be used to count the shifted data from  
--                   the ADCS7476 chip inside the PmocMIC board.
--   enShiftCounter: This signal will be used to enable the counter for the  
--                   shifted data from the ADCS7476 chip inside the PmocMIC.
--   enParalelLoad : This signal will be used to enable the load the shifted  
--                   data in a register.
--------------------------------------------------------------------------------

  type states is (Idle, ShiftIn, SyncData);

  signal current_state : states;
  signal next_state    : states;

  signal temp                    : std_logic_vector(15 downto 0);
  signal clk_en                  : std_logic;
  signal clk_counter             : unsigned(3 downto 0);
  signal shiftCounter            : unsigned(3 downto 0) := x"0";
  signal enShiftCounter          : std_logic;
  signal enParalelLoad           : std_logic;
  signal synch_START, started_ok : std_logic;

begin

--------------------------------------------------------------------------------
-- Title         : clock divider process
--
-- Description   : This is the process that will divide the 100 MHz clock 
--                 down to a clock speed of 12.5 MHz to drive the ADCS7476 chip. 
--------------------------------------------------------------------------------        
  clock_divide : process(rst, clk)
  begin
    if rst = '1' then
      clk_counter <= (others => '0');
    elsif (clk = '1' and clk'event) then
      clk_counter <= clk_counter + 1;
      synch_start <= (start or synch_start) and not started_ok;
    end if;
  end process;

  clk_en <= '1' when clk_counter(3 downto 0) = 0 else '0';
  SCLK   <= clk_counter(3);

-----------------------------------------------------------------------------------
--
-- Title      : counter
--
-- Description: This is the process were the converted data will be colected and
--              output.When the enShiftCounter is activated, the 16-bits of data  
--              from the ADCS7476 chip will be shifted inside the temporary 
--              registers. A 4-bit counter is used to keep shifting the data 
--              inside temp for 16 clock cycles. When the enParalelLoad
--              signal is generated inside the SyncData state, the converted data 
--              in the temporary shift registers will be placed on the output 
--              DATA
--    
-----------------------------------------------------------------------------------    

  counter : process(clk)
  begin
    if rising_edge(clk) then
      if clk_en = '1' then
        if (enShiftCounter = '1') then
          temp         <= temp(14 downto 0) & SDATA;
          shiftCounter <= shiftCounter + 1;
        elsif (enParalelLoad = '1') then
          shiftCounter <= "0000";
          DATA         <= temp(11 downto 0);
        end if;
      end if;
    end if;
  end process;
---------------------------------------------------------------------------------
--
-- Title      : Finite State Machine
--
-- Description: This 3 processes represent the FSM that contains three states.
--              The first state is the Idle state in which a temporary registers
--              is assigned the updated value of the input "DATA".
--              The next state is the ShiftIn state where the 16-bits of data
--              from the ADCS7476 chip are left shifted in the temp
--              shift register. The third state, SyncData drives the
--              output signal nCS high for 1 clock period maintainig nCS high  
--              also in the Idle state telling the ADCS7476 to mark the end of
--              the conversion.
-- Notes:         The data will change on the lower edge of the clock signal. Their 
--                     is also an asynchronous reset that will reset all signals to  
--                     their original state.
--
-----------------------------------------------------------------------------------        

-----------------------------------------------------------------------------------
--
-- Title      : SYNC_PROC
--
-- Description: This is the process were the states are changed synchronously. At 
--              reset the current state becomes Idle state.
--    
-----------------------------------------------------------------------------------            
  SYNC_PROC : process (clk)
  begin
    if rising_edge(clk) then
      if clk_en = '1' then
        if (rst = '1') then
          current_state <= Idle;
        else
          current_state <= next_state;
        end if;
      end if;
    end if;
  end process;

-----------------------------------------------------------------------------------
--
-- Title      : OUTPUT_DECODE
--
-- Description: This is the process were the output signals are generated
--              unsynchronously based on the state only (Moore State Machine).
--    
-----------------------------------------------------------------------------------        
  OUTPUT_DECODE : process (current_state)
  begin
    if current_state = Idle then
      enShiftCounter <= '0';
      DONE           <= '1';
      --nCS <='1';
      nCS            <= '1';
      enParalelLoad  <= '0';
    elsif current_state = ShiftIn then
      enShiftCounter <= '1';
      DONE           <= '0';
      --nCS <='0';
      nCS            <= '0';
      enParalelLoad  <= '0';
    else                                --if current_state = SyncData then
      enShiftCounter <= '0';
      DONE           <= '0';
      --nCS <='1';
      nCS            <= '1';
      enParalelLoad  <= '1';
    end if;
  end process;

----------------------------------------------------------------------------------
--
-- Title      : NEXT_STATE_DECODE
--
-- Description: This is the process were the next state logic is generated 
--              depending on the current state and the input signals.
--    
-----------------------------------------------------------------------------------    
  NEXT_STATE_DECODE : process (current_state, START, shiftCounter)
  begin

    next_state <= current_state;        -- default is to stay in current state
    started_ok <= '0';
    case (current_state) is
      when Idle =>
        if synch_START = '1' then
          next_state <= ShiftIn;
        end if;
      when ShiftIn =>
        started_ok <= '1';
        if shiftCounter = 15 then
          next_state <= SyncData;
        end if;
      when SyncData =>
        if START = '0' then
          next_state <= Idle;
        end if;
      when others =>
        next_state <= Idle;
    end case;
  end process;


end PmodMic;

// VHDL entity SpeakerCtrl, as the project stores it:
-------------------------------------------------------------------------
--    SpeakerCtrl.VHD
-------------------------------------------------------------------------
--    Author         : Andres Upegui
-- CopyRight 2023 HEPIA
-------------------------------------------------------------------------
--    Description : This file is the VHDL code for a PMOD I2S controller.
--
-------------------------------------------------------------------------
--    Revision History:
-- Dec/02/2023 LG (HEPIA): adapted for Basys3 (100MHz clock instead of 50)
-------------------------------------------------------------------------

library IEEE;
use IEEE.STD_LOGIC_1164.all;
use ieee.numeric_std.all;


entity SpeakerCtrl is
  port (clk      : in  std_logic;
        rst      : in  std_logic;
        Led      : out std_logic_vector (7 downto 0);
        audio_in : in  std_logic_vector(15 downto 0);
        done     : out std_logic;
        SDOUT    : out std_logic;
        SCLK     : out std_logic;
        MCLK     : out std_logic;
        LRCK     : out std_logic);
end SpeakerCtrl;

architecture Behavioral of SpeakerCtrl is

  signal div_cnt        : unsigned(11 downto 0);
  signal shift_reg_load : std_logic;
  signal shift_reg_en   : std_logic;
  signal shift_reg      : std_logic_vector(15 downto 0);

begin

------------------------------------    
---------- serial transmission -----
------------------------------------

  -- Generate LRCK and MCLK
  process(clk)
  begin
    if rising_edge(clk) then
      if rst = '1' then
        div_cnt <= (others => '0');
      else
        div_cnt <= div_cnt + 1;
      end if;
    end if;
  end process;

  LRCK <= div_cnt(11);                  -- 100 MHz / 2048 = 48'828.125 Hz
  MCLK <= div_cnt(5);                   -- 100 MHz / 32 = 3.125 MHz -> MCLK/LRCK = 64
  SCLK <= div_cnt(6);                   -- 100 MHz / 64 = 1.562500 MHz -> SCLK = 32 * Fs = 32 * LRCK

  shift_reg_load <= '1' when div_cnt(10 downto 0) = 0
                    else '0';

  done         <= shift_reg_load;
  shift_reg_en <= '1' when div_cnt(6 downto 0) = 0
                  else '0';

  SDOUT <= shift_reg(15);

  process(clk)
  begin
    if rising_edge(clk) then
      if rst = '1' then
        shift_reg <= (others => '0');
      elsif shift_reg_load = '1' then
        shift_reg <= audio_in;
      elsif shift_reg_en = '1' then
        shift_reg <= shift_reg(14 downto 0) & '0';
      end if;
    end if;
  end process;

  Led <= audio_in(13 downto 6);

end Behavioral;

// VHDL entity Overflow, as the project stores it:
--------------------------------------------------------------------------------
-- Project :
-- File    :
-- Autor   :
-- Date    :
--
--------------------------------------------------------------------------------
-- Description :
--
--------------------------------------------------------------------------------

LIBRARY ieee;
USE ieee.std_logic_1164.all;

ENTITY Overflow IS
  PORT (
  ------------------------------------------------------------------------------
  --Insert input ports below
    V_A 		: IN std_logic;
    V_B 		: IN std_logic;
    V_A_B 		: IN std_logic;
    N_A 		: IN std_logic;
    N_B 		: IN std_logic;
    N_A_B 		: IN std_logic;
  ------------------------------------------------------------------------------
  --Insert output ports below
    V_Res        : OUT std_logic;                    -- output bit example
    N_Res        : OUT std_logic;                    -- output bit example
    );
END Overflow;

--------------------------------------------------------------------------------
--Complete your VHDL description below
--------------------------------------------------------------------------------

ARCHITECTURE TypeArchitecture OF Overflow IS

BEGIN
	std_logic_vector Vect_A <= V_A & N_A;
	std_logic_vector Vect_B <= V_B & N_B;
	V_Res <= 1 when Vect_A = Vect_B else 0;
	N_Res <= 
END TypeArchitecture;
